// Logisim project cpu24-团队任务-2008092254.circ as structural Verilog: 13 circuits, main circuit ◇单周期MIPS+多级中断
module \电梯运行控制器  (
);

  wire \_1楼上 , \_1楼上_等待 , \_1楼下 , \_1楼下_等待 , \_1楼内 , \_1楼内_等待 , \_2楼上 , \_2楼上_等待 , \_2楼下 , \_2楼下_等待 , \_2楼内 ,
       \_2楼内_等待 , \_3楼上 , \_3楼上_等待 , \_3楼下 , \_3楼下_等待 , \_3楼内 , \_3楼内_等待 , \_4楼上 , \_4楼上_等待 , \_4楼下 ,
       \_4楼下_等待 , \_4楼内 , \_4楼内_等待 , \_5楼上 , \_5楼上_等待 , \_5楼下 , \_5楼下_等待 , \_5楼内 , \_5楼内_等待 , \_6楼上 ,
       \_6楼上_等待 , \_6楼下 , \_6楼下_等待 , \_6楼内 , \_6楼内_等待 , \_7楼上 , \_7楼上_等待 , \_7楼下 , \_7楼下_等待 , \_7楼内 ,
       \_7楼内_等待 , \_8楼上 , \_8楼上_等待 , \_8楼下 , \_8楼下_等待 , \_8楼内 , \_8楼内_等待 , \_9楼上 , \_9楼上_等待 , \_9楼下 ,
       \_9楼下_等待 , \_9楼内 , \_9楼内_等待 , \_10楼上 , \_10楼上_等待 , \_10楼下 , \_10楼下_等待 , \_10楼内 , \_10楼内_等待 , \_11楼上 ,
       \_11楼上_等待 , \_11楼下 , \_11楼下_等待 , \_11楼内 , \_11楼内_等待 , \_12楼上 , \_12楼上_等待 , \_12楼下 , \_12楼下_等待 ,
       \_12楼内 , \_12楼内_等待 , \_13楼上 , \_13楼上_等待 , \_13楼下 , \_13楼下_等待 , \_13楼内 , \_13楼内_等待 , \_14楼上 ,
       \_14楼上_等待 , \_14楼下 , \_14楼下_等待 , \_14楼内 , \_14楼内_等待 , \_15楼上 , \_15楼上_等待 , \_15楼下 , \_15楼下_等待 ,
       \_15楼内 , \_15楼内_等待 , \_16楼上 , \_16楼上_等待 , \_16楼下 , \_16楼下_等待 , \_16楼内 , \_16楼内_等待 , \_17楼上 ,
       \_17楼上_等待 , \_17楼下 , \_17楼下_等待 , \_17楼内 , \_17楼内_等待 , \_18楼上 , \_18楼上_等待 , \_18楼下 , \_18楼下_等待 ,
       \_18楼内 , \_18楼内_等待 , \_19楼上 , \_19楼上_等待 , \_19楼下 , \_19楼下_等待 , \_19楼内 , \_19楼内_等待 , \_20楼上 ,
       \_20楼上_等待 , \_20楼下 , \_20楼下_等待 , \_20楼内 , \_20楼内_等待 , \_21楼上 , \_21楼上_等待 , \_21楼下 , \_21楼下_等待 ,
       \_21楼内 , \_21楼内_等待 , \_22楼上 , \_22楼上_等待 , \_22楼下 , \_22楼下_等待 , \_22楼内 , \_22楼内_等待 , \_23楼上 ,
       \_23楼上_等待 , \_23楼下 , \_23楼下_等待 , \_23楼内 , \_23楼内_等待 , \_24楼上 , \_24楼上_等待 , \_24楼下 , \_24楼下_等待 ,
       \_24楼内 , \_24楼内_等待 , \_25楼上 , \_25楼上_等待 , \_25楼下 , \_25楼下_等待 , \_25楼内 , \_25楼内_等待 , \_26楼上 ,
       \_26楼上_等待 , \_26楼下 , \_26楼下_等待 , \_26楼内 , \_26楼内_等待 , \_27楼上 , \_27楼上_等待 , \_27楼下 , \_27楼下_等待 ,
       \_27楼内 , \_27楼内_等待 , \_28楼上 , \_28楼上_等待 , \_28楼下 , \_28楼下_等待 , \_28楼内 , \_28楼内_等待 , \_29楼上_等待 ,
       \_29楼下_等待 , \_29楼内_等待 , \_30楼上_等待 , \_30楼下_等待 , \_30楼内_等待 , \_31楼上_等待 , \_31楼下_等待 , \_31楼内_等待 ,
       \_32楼上_等待 , \_32楼下_等待 , \_32楼内_等待 , and_1_out, and_2_out, not_1_out, or_1_out, or_2_out, or_3_out,
       or_4_out, or_5_out, RST, \启动电动机 , \楼层按钮_1_out_97 , \楼层按钮_2_out_97 , \楼层按钮_3_out_97 ;
  wire [3:0] \十进制显示_1_out_2 , \十进制显示_1_out_3 ;
  wire [4:0] \当前楼层 , \当前楼层_q ;
  wire [15:0] \led控制信息_1_out_2 , \led控制信息_1_out_3 , \led控制信息_1_out_4 , \led控制信息_1_out_5 , \led控制信息_1_out_6 ,
       \led控制信息_1_out_7 , \led控制信息_1_out_8 , \led控制信息_1_out_9 , \led控制信息_1_out_10 , \led控制信息_1_out_11 ,
       \led控制信息_1_out_12 , \led控制信息_1_out_13 , \led控制信息_1_out_14 , \led控制信息_1_out_15 , \led控制信息_1_out_16 ,
       \led控制信息_1_out_17 ;
  wire [31:0] controlled_buffer_1_out, controlled_buffer_2_out, controlled_buffer_3_out, decoder_1_out31,
       decoder_2_out31, decoder_3_out31, \运行方向 ;

  Button \u_总复位  (.out(RST));
  Button button_1 (.out(\启动电动机 ));
  Button button_2 (.out(\_16楼内 ));
  Button button_3 (.out(\_15楼内 ));
  Button button_4 (.out(\_14楼内 ));
  Button button_5 (.out(\_13楼内 ));
  Button button_6 (.out(\_12楼内 ));
  Button button_7 (.out(\_11楼内 ));
  Button button_8 (.out(\_10楼内 ));
  Button button_9 (.out(\_9楼内 ));
  Button button_10 (.out(\_8楼内 ));
  Button button_11 (.out(\_7楼内 ));
  Button button_12 (.out(\_6楼内 ));
  Button button_13 (.out(\_5楼内 ));
  Button button_14 (.out(\_4楼内 ));
  Button button_15 (.out(\_3楼内 ));
  Button button_16 (.out(\_2楼内 ));
  Button button_17 (.out(\_1楼内 ));
  Hex_Digit_Display hex_digit_display_1 (.value(\十进制显示_1_out_2 ));  // open: dp
  \十进制显示  \u_十进制显示_1  (.in_1({{27{1'b0}}, \当前楼层 }), .out_2(\十进制显示_1_out_2 ), .out_3(\十进制显示_1_out_3 ));
  Decoder #(.select(5), .tristate("false"), .disabled("Z"), .enable("false")) decoder_1 (
    .out0(decoder_1_out31[31]), .out1(decoder_1_out31[30]), .out2(decoder_1_out31[29]),
    .out3(decoder_1_out31[28]), .out4(decoder_1_out31[27]), .out5(decoder_1_out31[26]),
    .out6(decoder_1_out31[25]), .out7(decoder_1_out31[24]), .out8(decoder_1_out31[23]),
    .out9(decoder_1_out31[22]), .out10(decoder_1_out31[21]), .out11(decoder_1_out31[20]),
    .out12(decoder_1_out31[19]), .out13(decoder_1_out31[18]), .out14(decoder_1_out31[17]),
    .out15(decoder_1_out31[16]), .out16(decoder_1_out31[15]), .out17(decoder_1_out31[14]),
    .out18(decoder_1_out31[13]), .out19(decoder_1_out31[12]), .out20(decoder_1_out31[11]),
    .out21(decoder_1_out31[10]), .out22(decoder_1_out31[9]), .out23(decoder_1_out31[8]),
    .out24(decoder_1_out31[7]), .out25(decoder_1_out31[6]), .out26(decoder_1_out31[5]),
    .out27(decoder_1_out31[4]), .out28(decoder_1_out31[3]), .out29(decoder_1_out31[2]),
    .out30(decoder_1_out31[1]), .out31(decoder_1_out31[0]), .sel(\当前楼层_q ));
  Hex_Digit_Display hex_digit_display_2 (.value(\十进制显示_1_out_3 ));  // open: dp
  LED #(.active("true")) led_1 (.in(\_16楼内_等待 ));
  LED #(.active("true")) led_2 (.in(\_15楼内_等待 ));
  LED #(.active("true")) led_3 (.in(\_14楼内_等待 ));
  LED #(.active("true")) led_4 (.in(\_13楼内_等待 ));
  LED #(.active("true")) led_5 (.in(\_12楼内_等待 ));
  LED #(.active("true")) led_6 (.in(\_11楼内_等待 ));
  LED #(.active("true")) led_7 (.in(\_10楼内_等待 ));
  LED #(.active("true")) led_8 (.in(\_9楼内_等待 ));
  LED #(.active("true")) led_9 (.in(\_8楼内_等待 ));
  LED #(.active("true")) led_10 (.in(\_7楼内_等待 ));
  LED #(.active("true")) led_11 (.in(\_6楼内_等待 ));
  LED #(.active("true")) led_12 (.in(\_5楼内_等待 ));
  LED #(.active("true")) led_13 (.in(\_4楼内_等待 ));
  LED #(.active("true")) led_14 (.in(\_3楼内_等待 ));
  LED #(.active("true")) led_15 (.in(\_2楼内_等待 ));
  LED #(.active("true")) led_16 (.in(\_1楼内_等待 ));
  assign controlled_buffer_1_out = 1'b1 ? decoder_1_out31 : 32'bz;  // Controlled_Buffer controlled_buffer_1
  \楼层按钮  \u_楼层按钮_1  (
    ._31(1'b0), ._30(1'b0), ._29(1'b0), ._28(1'b0), ._27(\_28楼内 ), ._26(\_27楼内 ), ._25(\_26楼内 ),
    ._24(\_25楼内 ), ._23(\_24楼内 ), ._22(\_23楼内 ), ._21(\_22楼内 ), ._20(\_21楼内 ), ._19(\_20楼内 ), ._18(\_19楼内 ),
    ._17(\_18楼内 ), ._16(\_17楼内 ), ._15(\_16楼内 ), ._14(\_15楼内 ), ._13(\_14楼内 ), ._12(\_13楼内 ), ._11(\_12楼内 ),
    ._10(\_11楼内 ), ._9(\_10楼内 ), ._8(\_9楼内 ), ._7(\_8楼内 ), ._6(\_7楼内 ), ._5(\_6楼内 ), ._4(\_5楼内 ),
    ._3(\_4楼内 ), ._2(\_3楼内 ), ._1(\_2楼内 ), ._0(\_1楼内 ), ._31_2(\_32楼内_等待 ),
    .\异步清零 (controlled_buffer_1_out[0]), ._30_2(\_31楼内_等待 ), .\异步清零_2 (controlled_buffer_1_out[1]),
    ._29_2(\_30楼内_等待 ), .\异步清零_3 (controlled_buffer_1_out[2]), ._28_2(\_29楼内_等待 ),
    .\异步清零_4 (controlled_buffer_1_out[3]), ._27_2(\_28楼内_等待 ), .\异步清零_5 (controlled_buffer_1_out[4]),
    ._26_2(\_27楼内_等待 ), .\异步清零_6 (controlled_buffer_1_out[5]), ._25_2(\_26楼内_等待 ),
    .\异步清零_7 (controlled_buffer_1_out[6]), ._24_2(\_25楼内_等待 ), .\异步清零_8 (controlled_buffer_1_out[7]),
    ._23_2(\_24楼内_等待 ), .\异步清零_9 (controlled_buffer_1_out[8]), ._22_2(\_23楼内_等待 ),
    .\异步清零_10 (controlled_buffer_1_out[9]), ._21_2(\_22楼内_等待 ), .\异步清零_11 (controlled_buffer_1_out[10]),
    ._20_2(\_21楼内_等待 ), .\异步清零_12 (controlled_buffer_1_out[11]), ._19_2(\_20楼内_等待 ),
    .\异步清零_13 (controlled_buffer_1_out[12]), ._18_2(\_19楼内_等待 ), .\异步清零_14 (controlled_buffer_1_out[13]),
    ._17_2(\_18楼内_等待 ), .\异步清零_15 (controlled_buffer_1_out[14]), ._16_2(\_17楼内_等待 ),
    .\异步清零_16 (controlled_buffer_1_out[15]), ._15_2(\_16楼内_等待 ), .\异步清零_17 (controlled_buffer_1_out[16]),
    ._14_2(\_15楼内_等待 ), .\异步清零_18 (controlled_buffer_1_out[17]), ._13_2(\_14楼内_等待 ),
    .\异步清零_19 (controlled_buffer_1_out[18]), ._12_2(\_13楼内_等待 ), .\异步清零_20 (controlled_buffer_1_out[19]),
    ._11_2(\_12楼内_等待 ), .\异步清零_21 (controlled_buffer_1_out[20]), ._10_2(\_11楼内_等待 ),
    .\异步清零_22 (controlled_buffer_1_out[21]), ._9_2(\_10楼内_等待 ), .\异步清零_23 (controlled_buffer_1_out[22]),
    ._8_2(\_9楼内_等待 ), .\异步清零_24 (controlled_buffer_1_out[23]), ._7_2(\_8楼内_等待 ),
    .\异步清零_25 (controlled_buffer_1_out[24]), ._6_2(\_7楼内_等待 ), .\异步清零_26 (controlled_buffer_1_out[25]),
    ._5_2(\_6楼内_等待 ), .\异步清零_27 (controlled_buffer_1_out[26]), ._4_2(\_5楼内_等待 ),
    .\异步清零_28 (controlled_buffer_1_out[27]), ._3_2(\_4楼内_等待 ), .\异步清零_29 (controlled_buffer_1_out[28]),
    ._2_2(\_3楼内_等待 ), .\异步清零_30 (controlled_buffer_1_out[29]), ._1_2(\_2楼内_等待 ),
    .\异步清零_31 (controlled_buffer_1_out[30]), ._0_2(\_1楼内_等待 ), .\异步清零_32 (controlled_buffer_1_out[31]),
    .out_97(\楼层按钮_1_out_97 ));
  Button button_18 (.out(\_28楼内 ));
  Button button_19 (.out(\_27楼内 ));
  Button button_20 (.out(\_26楼内 ));
  Button button_21 (.out(\_25楼内 ));
  Button button_22 (.out(\_24楼内 ));
  Button button_23 (.out(\_23楼内 ));
  Button button_24 (.out(\_22楼内 ));
  Button button_25 (.out(\_21楼内 ));
  Button button_26 (.out(\_20楼内 ));
  Button button_27 (.out(\_19楼内 ));
  Button button_28 (.out(\_18楼内 ));
  Button button_29 (.out(\_17楼内 ));
  DotMatrix #(.inputtype("column"), .matrixcols(16), .matrixrows(16), .persist(0), .dotshape("square")) dotmatrix_1 (
    .col0(\led控制信息_1_out_2 ), .col1(\led控制信息_1_out_3 ), .col2(\led控制信息_1_out_4 ), .col3(\led控制信息_1_out_5 ),
    .col4(\led控制信息_1_out_6 ), .col5(\led控制信息_1_out_7 ), .col6(\led控制信息_1_out_8 ), .col7(\led控制信息_1_out_9 ),
    .col8(\led控制信息_1_out_10 ), .col9(\led控制信息_1_out_11 ), .col10(\led控制信息_1_out_12 ),
    .col11(\led控制信息_1_out_13 ), .col12(\led控制信息_1_out_14 ), .col13(\led控制信息_1_out_15 ),
    .col14(\led控制信息_1_out_16 ), .col15(\led控制信息_1_out_17 ));
  \LED控制信息  \led控制信息_1  (
    .in_1(\运行方向 [1:0]), .out_2(\led控制信息_1_out_2 ), .out_3(\led控制信息_1_out_3 ), .out_4(\led控制信息_1_out_4 ),
    .out_5(\led控制信息_1_out_5 ), .out_6(\led控制信息_1_out_6 ), .out_7(\led控制信息_1_out_7 ),
    .out_8(\led控制信息_1_out_8 ), .out_9(\led控制信息_1_out_9 ), .out_10(\led控制信息_1_out_10 ),
    .out_11(\led控制信息_1_out_11 ), .out_12(\led控制信息_1_out_12 ), .out_13(\led控制信息_1_out_13 ),
    .out_14(\led控制信息_1_out_14 ), .out_15(\led控制信息_1_out_15 ), .out_16(\led控制信息_1_out_16 ),
    .out_17(\led控制信息_1_out_17 ));
  LED #(.active("true")) led_17 (.in(\_32楼内_等待 ));
  LED #(.active("true")) led_18 (.in(\_31楼内_等待 ));
  LED #(.active("true")) led_19 (.in(\_30楼内_等待 ));
  LED #(.active("true")) led_20 (.in(\_29楼内_等待 ));
  LED #(.active("true")) led_21 (.in(\_28楼内_等待 ));
  LED #(.active("true")) led_22 (.in(\_27楼内_等待 ));
  LED #(.active("true")) led_23 (.in(\_26楼内_等待 ));
  LED #(.active("true")) led_24 (.in(\_25楼内_等待 ));
  LED #(.active("true")) led_25 (.in(\_24楼内_等待 ));
  LED #(.active("true")) led_26 (.in(\_23楼内_等待 ));
  LED #(.active("true")) led_27 (.in(\_22楼内_等待 ));
  LED #(.active("true")) led_28 (.in(\_21楼内_等待 ));
  LED #(.active("true")) led_29 (.in(\_20楼内_等待 ));
  LED #(.active("true")) led_30 (.in(\_19楼内_等待 ));
  LED #(.active("true")) led_31 (.in(\_18楼内_等待 ));
  LED #(.active("true")) led_32 (.in(\_17楼内_等待 ));
  Button button_30 (.out(\_28楼下 ));
  Button button_31 (.out(\_27楼下 ));
  Button button_32 (.out(\_26楼下 ));
  Button button_33 (.out(\_25楼下 ));
  Button button_34 (.out(\_24楼下 ));
  Button button_35 (.out(\_23楼下 ));
  Button button_36 (.out(\_22楼下 ));
  Button button_37 (.out(\_21楼下 ));
  Button button_38 (.out(\_20楼下 ));
  Button button_39 (.out(\_19楼下 ));
  Button button_40 (.out(\_18楼下 ));
  Button button_41 (.out(\_17楼下 ));
  Button button_42 (.out(\_16楼下 ));
  Button button_43 (.out(\_15楼下 ));
  Button button_44 (.out(\_14楼下 ));
  Button button_45 (.out(\_13楼下 ));
  Button button_46 (.out(\_12楼下 ));
  Button button_47 (.out(\_11楼下 ));
  Button button_48 (.out(\_10楼下 ));
  Button button_49 (.out(\_9楼下 ));
  Button button_50 (.out(\_8楼下 ));
  Button button_51 (.out(\_7楼下 ));
  Button button_52 (.out(\_6楼下 ));
  Button button_53 (.out(\_5楼下 ));
  Button button_54 (.out(\_4楼下 ));
  Button button_55 (.out(\_3楼下 ));
  Button button_56 (.out(\_2楼下 ));
  Button button_57 (.out(\_1楼下 ));
  Button button_58 (.out(\_28楼上 ));
  Button button_59 (.out(\_27楼上 ));
  Button button_60 (.out(\_26楼上 ));
  Button button_61 (.out(\_25楼上 ));
  Button button_62 (.out(\_24楼上 ));
  Button button_63 (.out(\_23楼上 ));
  Button button_64 (.out(\_22楼上 ));
  Button button_65 (.out(\_21楼上 ));
  Button button_66 (.out(\_20楼上 ));
  Button button_67 (.out(\_19楼上 ));
  Button button_68 (.out(\_18楼上 ));
  Button button_69 (.out(\_17楼上 ));
  Button button_70 (.out(\_16楼上 ));
  Button button_71 (.out(\_15楼上 ));
  Button button_72 (.out(\_14楼上 ));
  Button button_73 (.out(\_13楼上 ));
  Button button_74 (.out(\_12楼上 ));
  Button button_75 (.out(\_11楼上 ));
  Button button_76 (.out(\_10楼上 ));
  Button button_77 (.out(\_9楼上 ));
  Button button_78 (.out(\_8楼上 ));
  Button button_79 (.out(\_7楼上 ));
  Button button_80 (.out(\_6楼上 ));
  Button button_81 (.out(\_5楼上 ));
  Button button_82 (.out(\_4楼上 ));
  Button button_83 (.out(\_3楼上 ));
  Button button_84 (.out(\_2楼上 ));
  Button button_85 (.out(\_1楼上 ));
  LED #(.active("true")) led_33 (.in(\_32楼下_等待 ));
  LED #(.active("true")) led_34 (.in(\_31楼下_等待 ));
  LED #(.active("true")) led_35 (.in(\_30楼下_等待 ));
  LED #(.active("true")) led_36 (.in(\_29楼下_等待 ));
  LED #(.active("true")) led_37 (.in(\_28楼下_等待 ));
  LED #(.active("true")) led_38 (.in(\_27楼下_等待 ));
  LED #(.active("true")) led_39 (.in(\_26楼下_等待 ));
  LED #(.active("true")) led_40 (.in(\_25楼下_等待 ));
  LED #(.active("true")) led_41 (.in(\_24楼下_等待 ));
  LED #(.active("true")) led_42 (.in(\_23楼下_等待 ));
  LED #(.active("true")) led_43 (.in(\_22楼下_等待 ));
  LED #(.active("true")) led_44 (.in(\_21楼下_等待 ));
  LED #(.active("true")) led_45 (.in(\_20楼下_等待 ));
  LED #(.active("true")) led_46 (.in(\_19楼下_等待 ));
  LED #(.active("true")) led_47 (.in(\_18楼下_等待 ));
  LED #(.active("true")) led_48 (.in(\_17楼下_等待 ));
  LED #(.active("true")) led_49 (.in(\_16楼下_等待 ));
  LED #(.active("true")) led_50 (.in(\_15楼下_等待 ));
  LED #(.active("true")) led_51 (.in(\_14楼下_等待 ));
  LED #(.active("true")) led_52 (.in(\_13楼下_等待 ));
  LED #(.active("true")) led_53 (.in(\_12楼下_等待 ));
  LED #(.active("true")) led_54 (.in(\_11楼下_等待 ));
  LED #(.active("true")) led_55 (.in(\_10楼下_等待 ));
  LED #(.active("true")) led_56 (.in(\_9楼下_等待 ));
  LED #(.active("true")) led_57 (.in(\_8楼下_等待 ));
  LED #(.active("true")) led_58 (.in(\_7楼下_等待 ));
  LED #(.active("true")) led_59 (.in(\_6楼下_等待 ));
  LED #(.active("true")) led_60 (.in(\_5楼下_等待 ));
  LED #(.active("true")) led_61 (.in(\_4楼下_等待 ));
  LED #(.active("true")) led_62 (.in(\_3楼下_等待 ));
  LED #(.active("true")) led_63 (.in(\_2楼下_等待 ));
  LED #(.active("true")) led_64 (.in(\_1楼下_等待 ));
  Decoder #(.select(5), .tristate("false"), .disabled("Z"), .enable("false")) decoder_2 (
    .out0(decoder_2_out31[31]), .out1(decoder_2_out31[30]), .out2(decoder_2_out31[29]),
    .out3(decoder_2_out31[28]), .out4(decoder_2_out31[27]), .out5(decoder_2_out31[26]),
    .out6(decoder_2_out31[25]), .out7(decoder_2_out31[24]), .out8(decoder_2_out31[23]),
    .out9(decoder_2_out31[22]), .out10(decoder_2_out31[21]), .out11(decoder_2_out31[20]),
    .out12(decoder_2_out31[19]), .out13(decoder_2_out31[18]), .out14(decoder_2_out31[17]),
    .out15(decoder_2_out31[16]), .out16(decoder_2_out31[15]), .out17(decoder_2_out31[14]),
    .out18(decoder_2_out31[13]), .out19(decoder_2_out31[12]), .out20(decoder_2_out31[11]),
    .out21(decoder_2_out31[10]), .out22(decoder_2_out31[9]), .out23(decoder_2_out31[8]),
    .out24(decoder_2_out31[7]), .out25(decoder_2_out31[6]), .out26(decoder_2_out31[5]),
    .out27(decoder_2_out31[4]), .out28(decoder_2_out31[3]), .out29(decoder_2_out31[2]),
    .out30(decoder_2_out31[1]), .out31(decoder_2_out31[0]), .sel(\当前楼层_q ));
  LED #(.active("true")) led_65 (.in(\_32楼上_等待 ));
  LED #(.active("true")) led_66 (.in(\_31楼上_等待 ));
  LED #(.active("true")) led_67 (.in(\_30楼上_等待 ));
  LED #(.active("true")) led_68 (.in(\_29楼上_等待 ));
  LED #(.active("true")) led_69 (.in(\_28楼上_等待 ));
  LED #(.active("true")) led_70 (.in(\_27楼上_等待 ));
  LED #(.active("true")) led_71 (.in(\_26楼上_等待 ));
  LED #(.active("true")) led_72 (.in(\_25楼上_等待 ));
  LED #(.active("true")) led_73 (.in(\_24楼上_等待 ));
  LED #(.active("true")) led_74 (.in(\_23楼上_等待 ));
  LED #(.active("true")) led_75 (.in(\_22楼上_等待 ));
  LED #(.active("true")) led_76 (.in(\_21楼上_等待 ));
  LED #(.active("true")) led_77 (.in(\_20楼上_等待 ));
  LED #(.active("true")) led_78 (.in(\_19楼上_等待 ));
  LED #(.active("true")) led_79 (.in(\_18楼上_等待 ));
  LED #(.active("true")) led_80 (.in(\_17楼上_等待 ));
  LED #(.active("true")) led_81 (.in(\_16楼上_等待 ));
  LED #(.active("true")) led_82 (.in(\_15楼上_等待 ));
  LED #(.active("true")) led_83 (.in(\_14楼上_等待 ));
  LED #(.active("true")) led_84 (.in(\_13楼上_等待 ));
  LED #(.active("true")) led_85 (.in(\_12楼上_等待 ));
  LED #(.active("true")) led_86 (.in(\_11楼上_等待 ));
  LED #(.active("true")) led_87 (.in(\_10楼上_等待 ));
  LED #(.active("true")) led_88 (.in(\_9楼上_等待 ));
  LED #(.active("true")) led_89 (.in(\_8楼上_等待 ));
  LED #(.active("true")) led_90 (.in(\_7楼上_等待 ));
  LED #(.active("true")) led_91 (.in(\_6楼上_等待 ));
  LED #(.active("true")) led_92 (.in(\_5楼上_等待 ));
  LED #(.active("true")) led_93 (.in(\_4楼上_等待 ));
  LED #(.active("true")) led_94 (.in(\_3楼上_等待 ));
  LED #(.active("true")) led_95 (.in(\_2楼上_等待 ));
  LED #(.active("true")) led_96 (.in(\_1楼上_等待 ));
  assign controlled_buffer_2_out = or_1_out ? decoder_2_out31 : 32'bz;  // Controlled_Buffer controlled_buffer_2
  \楼层按钮  \u_楼层按钮_2  (
    ._31(1'b0), ._30(1'b0), ._29(1'b0), ._28(1'b0), ._27(\_28楼下 ), ._26(\_27楼下 ), ._25(\_26楼下 ),
    ._24(\_25楼下 ), ._23(\_24楼下 ), ._22(\_23楼下 ), ._21(\_22楼下 ), ._20(\_21楼下 ), ._19(\_20楼下 ), ._18(\_19楼下 ),
    ._17(\_18楼下 ), ._16(\_17楼下 ), ._15(\_16楼下 ), ._14(\_15楼下 ), ._13(\_14楼下 ), ._12(\_13楼下 ), ._11(\_12楼下 ),
    ._10(\_11楼下 ), ._9(\_10楼下 ), ._8(\_9楼下 ), ._7(\_8楼下 ), ._6(\_7楼下 ), ._5(\_6楼下 ), ._4(\_5楼下 ),
    ._3(\_4楼下 ), ._2(\_3楼下 ), ._1(\_2楼下 ), ._0(\_1楼下 ), ._31_2(\_32楼下_等待 ),
    .\异步清零 (controlled_buffer_2_out[0]), ._30_2(\_31楼下_等待 ), .\异步清零_2 (controlled_buffer_2_out[1]),
    ._29_2(\_30楼下_等待 ), .\异步清零_3 (controlled_buffer_2_out[2]), ._28_2(\_29楼下_等待 ),
    .\异步清零_4 (controlled_buffer_2_out[3]), ._27_2(\_28楼下_等待 ), .\异步清零_5 (controlled_buffer_2_out[4]),
    ._26_2(\_27楼下_等待 ), .\异步清零_6 (controlled_buffer_2_out[5]), ._25_2(\_26楼下_等待 ),
    .\异步清零_7 (controlled_buffer_2_out[6]), ._24_2(\_25楼下_等待 ), .\异步清零_8 (controlled_buffer_2_out[7]),
    ._23_2(\_24楼下_等待 ), .\异步清零_9 (controlled_buffer_2_out[8]), ._22_2(\_23楼下_等待 ),
    .\异步清零_10 (controlled_buffer_2_out[9]), ._21_2(\_22楼下_等待 ), .\异步清零_11 (controlled_buffer_2_out[10]),
    ._20_2(\_21楼下_等待 ), .\异步清零_12 (controlled_buffer_2_out[11]), ._19_2(\_20楼下_等待 ),
    .\异步清零_13 (controlled_buffer_2_out[12]), ._18_2(\_19楼下_等待 ), .\异步清零_14 (controlled_buffer_2_out[13]),
    ._17_2(\_18楼下_等待 ), .\异步清零_15 (controlled_buffer_2_out[14]), ._16_2(\_17楼下_等待 ),
    .\异步清零_16 (controlled_buffer_2_out[15]), ._15_2(\_16楼下_等待 ), .\异步清零_17 (controlled_buffer_2_out[16]),
    ._14_2(\_15楼下_等待 ), .\异步清零_18 (controlled_buffer_2_out[17]), ._13_2(\_14楼下_等待 ),
    .\异步清零_19 (controlled_buffer_2_out[18]), ._12_2(\_13楼下_等待 ), .\异步清零_20 (controlled_buffer_2_out[19]),
    ._11_2(\_12楼下_等待 ), .\异步清零_21 (controlled_buffer_2_out[20]), ._10_2(\_11楼下_等待 ),
    .\异步清零_22 (controlled_buffer_2_out[21]), ._9_2(\_10楼下_等待 ), .\异步清零_23 (controlled_buffer_2_out[22]),
    ._8_2(\_9楼下_等待 ), .\异步清零_24 (controlled_buffer_2_out[23]), ._7_2(\_8楼下_等待 ),
    .\异步清零_25 (controlled_buffer_2_out[24]), ._6_2(\_7楼下_等待 ), .\异步清零_26 (controlled_buffer_2_out[25]),
    ._5_2(\_6楼下_等待 ), .\异步清零_27 (controlled_buffer_2_out[26]), ._4_2(\_5楼下_等待 ),
    .\异步清零_28 (controlled_buffer_2_out[27]), ._3_2(\_4楼下_等待 ), .\异步清零_29 (controlled_buffer_2_out[28]),
    ._2_2(\_3楼下_等待 ), .\异步清零_30 (controlled_buffer_2_out[29]), ._1_2(\_2楼下_等待 ),
    .\异步清零_31 (controlled_buffer_2_out[30]), ._0_2(\_1楼下_等待 ), .\异步清零_32 (controlled_buffer_2_out[31]),
    .out_97(\楼层按钮_2_out_97 ));
  or or_1 (or_1_out, not_1_out, and_1_out);
  Decoder #(.select(5), .tristate("false"), .disabled("Z"), .enable("false")) decoder_3 (
    .out0(decoder_3_out31[31]), .out1(decoder_3_out31[30]), .out2(decoder_3_out31[29]),
    .out3(decoder_3_out31[28]), .out4(decoder_3_out31[27]), .out5(decoder_3_out31[26]),
    .out6(decoder_3_out31[25]), .out7(decoder_3_out31[24]), .out8(decoder_3_out31[23]),
    .out9(decoder_3_out31[22]), .out10(decoder_3_out31[21]), .out11(decoder_3_out31[20]),
    .out12(decoder_3_out31[19]), .out13(decoder_3_out31[18]), .out14(decoder_3_out31[17]),
    .out15(decoder_3_out31[16]), .out16(decoder_3_out31[15]), .out17(decoder_3_out31[14]),
    .out18(decoder_3_out31[13]), .out19(decoder_3_out31[12]), .out20(decoder_3_out31[11]),
    .out21(decoder_3_out31[10]), .out22(decoder_3_out31[9]), .out23(decoder_3_out31[8]),
    .out24(decoder_3_out31[7]), .out25(decoder_3_out31[6]), .out26(decoder_3_out31[5]),
    .out27(decoder_3_out31[4]), .out28(decoder_3_out31[3]), .out29(decoder_3_out31[2]),
    .out30(decoder_3_out31[1]), .out31(decoder_3_out31[0]), .sel(\当前楼层_q ));
  assign controlled_buffer_3_out = or_4_out ? decoder_3_out31 : 32'bz;  // Controlled_Buffer controlled_buffer_3
  \楼层按钮  \u_楼层按钮_3  (
    ._31(1'b0), ._30(1'b0), ._29(1'b0), ._28(1'b0), ._27(\_28楼上 ), ._26(\_27楼上 ), ._25(\_26楼上 ),
    ._24(\_25楼上 ), ._23(\_24楼上 ), ._22(\_23楼上 ), ._21(\_22楼上 ), ._20(\_21楼上 ), ._19(\_20楼上 ), ._18(\_19楼上 ),
    ._17(\_18楼上 ), ._16(\_17楼上 ), ._15(\_16楼上 ), ._14(\_15楼上 ), ._13(\_14楼上 ), ._12(\_13楼上 ), ._11(\_12楼上 ),
    ._10(\_11楼上 ), ._9(\_10楼上 ), ._8(\_9楼上 ), ._7(\_8楼上 ), ._6(\_7楼上 ), ._5(\_6楼上 ), ._4(\_5楼上 ),
    ._3(\_4楼上 ), ._2(\_3楼上 ), ._1(\_2楼上 ), ._0(\_1楼上 ), ._31_2(\_32楼上_等待 ),
    .\异步清零 (controlled_buffer_3_out[0]), ._30_2(\_31楼上_等待 ), .\异步清零_2 (controlled_buffer_3_out[1]),
    ._29_2(\_30楼上_等待 ), .\异步清零_3 (controlled_buffer_3_out[2]), ._28_2(\_29楼上_等待 ),
    .\异步清零_4 (controlled_buffer_3_out[3]), ._27_2(\_28楼上_等待 ), .\异步清零_5 (controlled_buffer_3_out[4]),
    ._26_2(\_27楼上_等待 ), .\异步清零_6 (controlled_buffer_3_out[5]), ._25_2(\_26楼上_等待 ),
    .\异步清零_7 (controlled_buffer_3_out[6]), ._24_2(\_25楼上_等待 ), .\异步清零_8 (controlled_buffer_3_out[7]),
    ._23_2(\_24楼上_等待 ), .\异步清零_9 (controlled_buffer_3_out[8]), ._22_2(\_23楼上_等待 ),
    .\异步清零_10 (controlled_buffer_3_out[9]), ._21_2(\_22楼上_等待 ), .\异步清零_11 (controlled_buffer_3_out[10]),
    ._20_2(\_21楼上_等待 ), .\异步清零_12 (controlled_buffer_3_out[11]), ._19_2(\_20楼上_等待 ),
    .\异步清零_13 (controlled_buffer_3_out[12]), ._18_2(\_19楼上_等待 ), .\异步清零_14 (controlled_buffer_3_out[13]),
    ._17_2(\_18楼上_等待 ), .\异步清零_15 (controlled_buffer_3_out[14]), ._16_2(\_17楼上_等待 ),
    .\异步清零_16 (controlled_buffer_3_out[15]), ._15_2(\_16楼上_等待 ), .\异步清零_17 (controlled_buffer_3_out[16]),
    ._14_2(\_15楼上_等待 ), .\异步清零_18 (controlled_buffer_3_out[17]), ._13_2(\_14楼上_等待 ),
    .\异步清零_19 (controlled_buffer_3_out[18]), ._12_2(\_13楼上_等待 ), .\异步清零_20 (controlled_buffer_3_out[19]),
    ._11_2(\_12楼上_等待 ), .\异步清零_21 (controlled_buffer_3_out[20]), ._10_2(\_11楼上_等待 ),
    .\异步清零_22 (controlled_buffer_3_out[21]), ._9_2(\_10楼上_等待 ), .\异步清零_23 (controlled_buffer_3_out[22]),
    ._8_2(\_9楼上_等待 ), .\异步清零_24 (controlled_buffer_3_out[23]), ._7_2(\_8楼上_等待 ),
    .\异步清零_25 (controlled_buffer_3_out[24]), ._6_2(\_7楼上_等待 ), .\异步清零_26 (controlled_buffer_3_out[25]),
    ._5_2(\_6楼上_等待 ), .\异步清零_27 (controlled_buffer_3_out[26]), ._4_2(\_5楼上_等待 ),
    .\异步清零_28 (controlled_buffer_3_out[27]), ._3_2(\_4楼上_等待 ), .\异步清零_29 (controlled_buffer_3_out[28]),
    ._2_2(\_3楼上_等待 ), .\异步清零_30 (controlled_buffer_3_out[29]), ._1_2(\_2楼上_等待 ),
    .\异步清零_31 (controlled_buffer_3_out[30]), ._0_2(\_1楼上_等待 ), .\异步清零_32 (controlled_buffer_3_out[31]),
    .out_97(\楼层按钮_3_out_97 ));
  Counter #(.width(5), .max('h1f), .ongoal("wrap"), .trigger("rising"), .behavior("new")) \u_当前楼层  (
    .Q(\当前楼层_q ), .clk(or_2_out), .clr(RST), .down(and_1_out));  // open: load, D, count, carry, preset
  or or_2 (or_2_out, and_1_out, and_2_out);
  and and_1 (and_1_out, \运行方向 [1], \启动电动机 );
  or or_3 (or_3_out, \楼层按钮_3_out_97 , \楼层按钮_2_out_97 , \楼层按钮_1_out_97 , or_2_out);
  and and_2 (and_2_out, \启动电动机 , \运行方向 [0]);
  \单周期MIPS_多级中断  \u_单周期mips_多级中断_1  (
    .LedData(\运行方向 ),
    .\输入数据0_向上 ({\_32楼上_等待 , \_31楼上_等待 , \_30楼上_等待 , \_29楼上_等待 , \_28楼上_等待 , \_27楼上_等待 , \_26楼上_等待 , \_25楼上_等待 , \_24楼上_等待 , \_23楼上_等待 , \_22楼上_等待 , \_21楼上_等待 , \_20楼上_等待 , \_19楼上_等待 , \_18楼上_等待 , \_17楼上_等待 , \_16楼上_等待 , \_15楼上_等待 , \_14楼上_等待 , \_13楼上_等待 , \_12楼上_等待 , \_11楼上_等待 , \_10楼上_等待 , \_9楼上_等待 , \_8楼上_等待 , \_7楼上_等待 , \_6楼上_等待 , \_5楼上_等待 , \_4楼上_等待 , \_3楼上_等待 , \_2楼上_等待 , \_1楼上_等待 }),
    .\输入数据1_向下 ({\_32楼下_等待 , \_31楼下_等待 , \_30楼下_等待 , \_29楼下_等待 , \_28楼下_等待 , \_27楼下_等待 , \_26楼下_等待 , \_25楼下_等待 , \_24楼下_等待 , \_23楼下_等待 , \_22楼下_等待 , \_21楼下_等待 , \_20楼下_等待 , \_19楼下_等待 , \_18楼下_等待 , \_17楼下_等待 , \_16楼下_等待 , \_15楼下_等待 , \_14楼下_等待 , \_13楼下_等待 , \_12楼下_等待 , \_11楼下_等待 , \_10楼下_等待 , \_9楼下_等待 , \_8楼下_等待 , \_7楼下_等待 , \_6楼下_等待 , \_5楼下_等待 , \_4楼下_等待 , \_3楼下_等待 , \_2楼下_等待 , \_1楼下_等待 }),
    .\输入数据2_内部 ({\_32楼内_等待 , \_31楼内_等待 , \_30楼内_等待 , \_29楼内_等待 , \_28楼内_等待 , \_27楼内_等待 , \_26楼内_等待 , \_25楼内_等待 , \_24楼内_等待 , \_23楼内_等待 , \_22楼内_等待 , \_21楼内_等待 , \_20楼内_等待 , \_19楼内_等待 , \_18楼内_等待 , \_17楼内_等待 , \_16楼内_等待 , \_15楼内_等待 , \_14楼内_等待 , \_13楼内_等待 , \_12楼内_等待 , \_11楼内_等待 , \_10楼内_等待 , \_9楼内_等待 , \_8楼内_等待 , \_7楼内_等待 , \_6楼内_等待 , \_5楼内_等待 , \_4楼内_等待 , \_3楼内_等待 , \_2楼内_等待 , \_1楼内_等待 }),
    .\输入数据3_当前楼层 ({{27{1'b0}}, \当前楼层 }), .\电动机运行_电梯关门 (or_3_out), .\总复位 (RST));
  Adder #(.width(5)) adder_1 (.a(5'b00001), .b(\当前楼层_q ), .out(\当前楼层 ), .cin(1'b0));  // open: cout
  or or_4 (or_4_out, and_2_out, not_1_out);
  not not_1 (not_1_out, or_5_out);
  or or_5 (or_5_out, \运行方向 [1], \运行方向 [0]);

  // Notes on the sheet:
  //   使能
  //   电梯中按了的楼层
  //   按了“上升”按钮的楼层
endmodule

module \楼层按钮  (
  input  _31,
  input  \异步清零 ,
  input  _30,
  input  \异步清零_2 ,
  input  _29,
  input  \异步清零_3 ,
  input  _28,
  input  \异步清零_4 ,
  input  _27,
  input  \异步清零_5 ,
  input  _26,
  input  \异步清零_6 ,
  input  _25,
  input  \异步清零_7 ,
  input  _24,
  input  \异步清零_8 ,
  input  _23,
  input  \异步清零_9 ,
  input  _22,
  input  \异步清零_10 ,
  input  _21,
  input  \异步清零_11 ,
  input  _20,
  input  \异步清零_12 ,
  input  _19,
  input  \异步清零_13 ,
  input  _18,
  input  \异步清零_14 ,
  input  _17,
  input  \异步清零_15 ,
  input  _16,
  input  \异步清零_16 ,
  input  _15,
  input  \异步清零_17 ,
  input  _14,
  input  \异步清零_18 ,
  input  _13,
  input  \异步清零_19 ,
  input  _12,
  input  \异步清零_20 ,
  input  _11,
  input  \异步清零_21 ,
  input  _10,
  input  \异步清零_22 ,
  input  _9,
  input  \异步清零_23 ,
  input  _8,
  input  \异步清零_24 ,
  input  _7,
  input  \异步清零_25 ,
  input  _6,
  input  \异步清零_26 ,
  input  _5,
  input  \异步清零_27 ,
  input  _4,
  input  \异步清零_28 ,
  input  _3,
  input  \异步清零_29 ,
  input  _2,
  input  \异步清零_30 ,
  input  _1,
  input  \异步清零_31 ,
  input  _0,
  input  \异步清零_32 ,
  output _31_2,
  output _30_2,
  output _29_2,
  output _28_2,
  output _27_2,
  output _26_2,
  output _25_2,
  output _24_2,
  output _23_2,
  output _22_2,
  output _21_2,
  output _20_2,
  output _19_2,
  output _18_2,
  output _17_2,
  output _16_2,
  output _15_2,
  output _14_2,
  output _13_2,
  output _12_2,
  output _11_2,
  output _10_2,
  output _9_2,
  output _8_2,
  output _7_2,
  output _6_2,
  output _5_2,
  output _4_2,
  output _3_2,
  output _2_2,
  output _1_2,
  output _0_2,
  output out_97
);

  or or_1 (out_97, _31, _30, _29, _28, _27, _26, _25, _24, _23, _22, _21, _20, _19, _18, _17, _16, _15, _14, _13, _12, _11, _10, _9, _8, _7, _6, _5, _4, _3, _2, _1, _0);
  Register #(.width(1), .trigger("rising"), .Select("low")) register_1 (
    .D(_31), .Q(_31_2), .clk(_31), .clr(\异步清零 ));  // open: en
  Register #(.width(1), .trigger("rising"), .Select("low")) register_2 (
    .D(_30), .Q(_30_2), .clk(_30), .clr(\异步清零_2 ));  // open: en
  Register #(.width(1), .trigger("rising"), .Select("low")) register_3 (
    .D(_29), .Q(_29_2), .clk(_29), .clr(\异步清零_3 ));  // open: en
  Register #(.width(1), .trigger("rising"), .Select("low")) register_4 (
    .D(_28), .Q(_28_2), .clk(_28), .clr(\异步清零_4 ));  // open: en
  Register #(.width(1), .trigger("rising"), .Select("low")) register_5 (
    .D(_27), .Q(_27_2), .clk(_27), .clr(\异步清零_5 ));  // open: en
  Register #(.width(1), .trigger("rising"), .Select("low")) register_6 (
    .D(_26), .Q(_26_2), .clk(_26), .clr(\异步清零_6 ));  // open: en
  Register #(.width(1), .trigger("rising"), .Select("low")) register_7 (
    .D(_25), .Q(_25_2), .clk(_25), .clr(\异步清零_7 ));  // open: en
  Register #(.width(1), .trigger("rising"), .Select("low")) register_8 (
    .D(_24), .Q(_24_2), .clk(_24), .clr(\异步清零_8 ));  // open: en
  Register #(.width(1), .trigger("rising"), .Select("low")) register_9 (
    .D(_23), .Q(_23_2), .clk(_23), .clr(\异步清零_9 ));  // open: en
  Register #(.width(1), .trigger("rising"), .Select("low")) register_10 (
    .D(_22), .Q(_22_2), .clk(_22), .clr(\异步清零_10 ));  // open: en
  Register #(.width(1), .trigger("rising"), .Select("low")) register_11 (
    .D(_21), .Q(_21_2), .clk(_21), .clr(\异步清零_11 ));  // open: en
  Register #(.width(1), .trigger("rising"), .Select("low")) register_12 (
    .D(_20), .Q(_20_2), .clk(_20), .clr(\异步清零_12 ));  // open: en
  Register #(.width(1), .trigger("rising"), .Select("low")) register_13 (
    .D(_19), .Q(_19_2), .clk(_19), .clr(\异步清零_13 ));  // open: en
  Register #(.width(1), .trigger("rising"), .Select("low")) register_14 (
    .D(_18), .Q(_18_2), .clk(_18), .clr(\异步清零_14 ));  // open: en
  Register #(.width(1), .trigger("rising"), .Select("low")) register_15 (
    .D(_17), .Q(_17_2), .clk(_17), .clr(\异步清零_15 ));  // open: en
  Register #(.width(1), .trigger("rising"), .Select("low")) register_16 (
    .D(_16), .Q(_16_2), .clk(_16), .clr(\异步清零_16 ));  // open: en
  Register #(.width(1), .trigger("rising"), .Select("low")) register_17 (
    .D(_15), .Q(_15_2), .clk(_15), .clr(\异步清零_17 ));  // open: en
  Register #(.width(1), .trigger("rising"), .Select("low")) register_18 (
    .D(_14), .Q(_14_2), .clk(_14), .clr(\异步清零_18 ));  // open: en
  Register #(.width(1), .trigger("rising"), .Select("low")) register_19 (
    .D(_13), .Q(_13_2), .clk(_13), .clr(\异步清零_19 ));  // open: en
  Register #(.width(1), .trigger("rising"), .Select("low")) register_20 (
    .D(_12), .Q(_12_2), .clk(_12), .clr(\异步清零_20 ));  // open: en
  Register #(.width(1), .trigger("rising"), .Select("low")) register_21 (
    .D(_11), .Q(_11_2), .clk(_11), .clr(\异步清零_21 ));  // open: en
  Register #(.width(1), .trigger("rising"), .Select("low")) register_22 (
    .D(_10), .Q(_10_2), .clk(_10), .clr(\异步清零_22 ));  // open: en
  Register #(.width(1), .trigger("rising"), .Select("low")) register_23 (
    .D(_9), .Q(_9_2), .clk(_9), .clr(\异步清零_23 ));  // open: en
  Register #(.width(1), .trigger("rising"), .Select("low")) register_24 (
    .D(_8), .Q(_8_2), .clk(_8), .clr(\异步清零_24 ));  // open: en
  Register #(.width(1), .trigger("rising"), .Select("low")) register_25 (
    .D(_7), .Q(_7_2), .clk(_7), .clr(\异步清零_25 ));  // open: en
  Register #(.width(1), .trigger("rising"), .Select("low")) register_26 (
    .D(_6), .Q(_6_2), .clk(_6), .clr(\异步清零_26 ));  // open: en
  Register #(.width(1), .trigger("rising"), .Select("low")) register_27 (
    .D(_5), .Q(_5_2), .clk(_5), .clr(\异步清零_27 ));  // open: en
  Register #(.width(1), .trigger("rising"), .Select("low")) register_28 (
    .D(_4), .Q(_4_2), .clk(_4), .clr(\异步清零_28 ));  // open: en
  Register #(.width(1), .trigger("rising"), .Select("low")) register_29 (
    .D(_3), .Q(_3_2), .clk(_3), .clr(\异步清零_29 ));  // open: en
  Register #(.width(1), .trigger("rising"), .Select("low")) register_30 (
    .D(_2), .Q(_2_2), .clk(_2), .clr(\异步清零_30 ));  // open: en
  Register #(.width(1), .trigger("rising"), .Select("low")) register_31 (
    .D(_1), .Q(_1_2), .clk(_1), .clr(\异步清零_31 ));  // open: en
  Register #(.width(1), .trigger("rising"), .Select("low")) register_32 (
    .D(_0), .Q(_0_2), .clk(_0), .clr(\异步清零_32 ));  // open: en
endmodule

module \LED控制信息  (
  input  [1:0] in_1,
  output [15:0] out_2,
  output [15:0] out_3,
  output [15:0] out_4,
  output [15:0] out_5,
  output [15:0] out_6,
  output [15:0] out_7,
  output [15:0] out_8,
  output [15:0] out_9,
  output [15:0] out_10,
  output [15:0] out_11,
  output [15:0] out_12,
  output [15:0] out_13,
  output [15:0] out_14,
  output [15:0] out_15,
  output [15:0] out_16,
  output [15:0] out_17
);

  Multiplexer #(.select(2), .width(16), .disabled("Z"), .enable("false")) multiplexer_1 (
    .in0(16'h800), .in1(16'h1), .in2(16'h8000), .in3({16{1'b0}}), .out(out_2), .sel(in_1));
  Multiplexer #(.select(2), .width(16), .disabled("Z"), .enable("false")) multiplexer_2 (
    .in0(16'h800), .in1(16'h1), .in2(16'h8000), .in3({16{1'b0}}), .out(out_3), .sel(in_1));
  Multiplexer #(.select(2), .width(16), .disabled("Z"), .enable("false")) multiplexer_3 (
    .in0(16'h1fff), .in1(16'h1), .in2(16'h8000), .in3({16{1'b0}}), .out(out_4), .sel(in_1));
  Multiplexer #(.select(2), .width(16), .disabled("Z"), .enable("false")) multiplexer_4 (
    .in0(16'h2000), .in1(16'h1), .in2(16'h8000), .in3({16{1'b0}}), .out(out_5), .sel(in_1));
  Multiplexer #(.select(2), .width(16), .disabled("Z"), .enable("false")) multiplexer_5 (
    .in0(16'h4000), .in1({16{1'b1}}), .in2(16'h8000), .in3({16{1'b0}}), .out(out_6), .sel(in_1));
  Multiplexer #(.select(2), .width(16), .disabled("Z"), .enable("false")) multiplexer_6 (
    .in0(16'h8000), .in1(16'h201), .in2({16{1'b1}}), .in3({16{1'b0}}), .out(out_7), .sel(in_1));
  Multiplexer #(.select(2), .width(16), .disabled("Z"), .enable("false")) multiplexer_7 (
    .in0(16'h20c0), .in1(16'h201), .in2(16'h8800), .in3({16{1'b0}}), .out(out_8), .sel(in_1));
  Multiplexer #(.select(2), .width(16), .disabled("Z"), .enable("false")) multiplexer_8 (
    .in0(16'h2082), .in1(16'h201), .in2(16'h8800), .in3({16{1'b0}}), .out(out_9), .sel(in_1));
  Multiplexer #(.select(2), .width(16), .disabled("Z"), .enable("false")) multiplexer_9 (
    .in0(16'h2ea1), .in1(16'h201), .in2(16'h8400), .in3({16{1'b0}}), .out(out_10), .sel(in_1));
  Multiplexer #(.select(2), .width(16), .disabled("Z"), .enable("false")) multiplexer_10 (
    .in0(16'h2aa1), .in1(16'h201), .in2(16'h8200), .in3({16{1'b0}}), .out(out_11), .sel(in_1));
  Multiplexer #(.select(2), .width(16), .disabled("Z"), .enable("false")) multiplexer_11 (
    .in0(16'haabf), .in1(16'h201), .in2(16'h8100), .in3({16{1'b0}}), .out(out_12), .sel(in_1));
  Multiplexer #(.select(2), .width(16), .disabled("Z"), .enable("false")) multiplexer_12 (
    .in0(16'h6aa0), .in1(16'h201), .in2(16'h8000), .in3({16{1'b0}}), .out(out_13), .sel(in_1));
  Multiplexer #(.select(2), .width(16), .disabled("Z"), .enable("false")) multiplexer_13 (
    .in0(16'h2ea0), .in1(16'h1), .in2(16'h8000), .in3({16{1'b0}}), .out(out_14), .sel(in_1));
  Multiplexer #(.select(2), .width(16), .disabled("Z"), .enable("false")) multiplexer_14 (
    .in0(16'h2080), .in1(16'h1), .in2(16'h8000), .in3({16{1'b0}}), .out(out_15), .sel(in_1));
  Multiplexer #(.select(2), .width(16), .disabled("Z"), .enable("false")) multiplexer_15 (
    .in0(16'h20c0), .in1(16'h1), .in2(16'h8000), .in3({16{1'b0}}), .out(out_16), .sel(in_1));
  Multiplexer #(.select(2), .width(16), .disabled("Z"), .enable("false")) multiplexer_16 (
    .in0({16{1'b0}}), .in1(16'h1), .in2(16'h8000), .in3({16{1'b0}}), .out(out_17), .sel(in_1));
endmodule

module \十进制显示  (
  input  [31:0] in_1,
  output [3:0] out_2,
  output [3:0] out_3
);

  wire [4:4] divider_1_out, divider_1_rem;

  Divider #(.width(5)) divider_1 (
    .a(in_1[4:0]), .b(5'b01010), .out({divider_1_out[4], out_2}), .upper({5{1'b0}}),
    .rem({divider_1_rem[4], out_3}));
endmodule

module \单周期MIPS_多级中断  (
  input  \电动机运行_电梯关门 ,
  input  \总复位 ,
  input  [31:0] \输入数据0_向上 ,
  input  [31:0] \输入数据1_向下 ,
  input  [31:0] \输入数据2_内部 ,
  input  [31:0] \输入数据3_当前楼层 ,
  output [31:0] LedData
);

  wire and_1_out, and_2_out, and_3_out, and_4_out, and_5_out, and_6_out, and_7_out, and_8_out, and_9_out,
       and_10_out, and_11_out, and_12_out, and_13_out, and_14_out, and_15_out, and_16_out, and_17_out,
       and_18_out, and_20_out, and_21_out, CLK, comparator_1_eq, d_ff_1_q, d_ff_2_q, d_ff_3_q, d_ff_4_q,
       d_ff_4_qn, decoder_1_out0, decoder_1_out1, decoder_1_out2, Go, IE_qn, IR1, IR1_q, IR2, IR2_q, IR3,
       IR3_q, IRC, LedNew, LoadIn, \mcop辅助译码器_1_mfepc , \mcop辅助译码器_1_mtepc , \mcop辅助译码器_1_mtie , MemWrite,
       mips_alu_1_equal, not_1_out, not_2_out, not_3_out, not_4_out, or_4_out, or_5_out, or_6_out, or_7_out,
       or_8_out, or_12_out, or_14_out, or_15_out, or_16_out, or_17_out, priority_encoder_1_gs, RegWrite,
       SignedExt, VarShift, W1, W2, W3, \中断1服务中_q , \中断1服务中_qn , \中断2服务中_q , \中断2服务中_qn , \中断3服务中_q ,
       \中断3服务中_qn , \单周期硬布线控制器_4_三级中断_1_alu_src , \单周期硬布线控制器_4_三级中断_1_beq , \单周期硬布线控制器_4_三级中断_1_bgtz ,
       \单周期硬布线控制器_4_三级中断_1_bne , \单周期硬布线控制器_4_三级中断_1_eret , \单周期硬布线控制器_4_三级中断_1_jal ,
       \单周期硬布线控制器_4_三级中断_1_jmp , \单周期硬布线控制器_4_三级中断_1_jr , \单周期硬布线控制器_4_三级中断_1_mcop ,
       \单周期硬布线控制器_4_三级中断_1_memtoreg , \单周期硬布线控制器_4_三级中断_1_regdst , \单周期硬布线控制器_4_三级中断_1_regwrite ,
       \单周期硬布线控制器_4_三级中断_1_syscall ;
  wire [1:0] priority_encoder_1_out;
  wire [3:0] \单周期硬布线控制器_4_三级中断_1_alu_op ;
  wire [4:0] multiplexer_5_out, multiplexer_6_out, multiplexer_7_out, multiplexer_10_out, multiplexer_11_out,
       multiplexer_14_out;
  wire [15:0] \总周期数 ;
  wire [27:0] bit_extender_3_out, shifter_2_out;
  wire [31:0] adder_1_out, adder_2_out, bit_extender_1_out, bit_extender_2_out, EPC_q, IR, MDin, MenOut,
       mips_alu_1_result, mips_regifile_1_r1, multiplexer_1_out, multiplexer_2_out, multiplexer_3_out,
       multiplexer_4_out, multiplexer_8_out, multiplexer_12_out, multiplexer_13_out, multiplexer_15_out,
       multiplexer_16_out, multiplexer_17_out, multiplexer_18_out, multiplexer_20_out, PC, ram_1_data, RDin,
       shifter_1_out;

  Clock #(.highDuration(1), .lowDuration(1)) clock_1 (.out(CLK));
  Button _1 ();  // open: out
  Button _2 ();  // open: out
  Button _3 (.out(IRC));
  Button \u_继续运行  (.out(Go));
  LED #(.active("true")) led_1 (.in(W1));
  LED #(.active("true")) led_2 (.in(W2));
  LED #(.active("true")) led_3 (.in(W3));
  Hex_Digit_Display hex_digit_display_1 (.value(LedData[31:28]));  // open: dp
  D_Flip_Flop #(.trigger("rising"), .Pre_Clr_Positions("LEGACY"), .NegatePresetClear("false"), .enable("true"), .NewFFLayout("false")) d_ff_1 (
    .clk(IR1), .D(1'b1), .Q(d_ff_1_q), .reset(IR1_q));  // open: Qn, preset, en
  or or_1 (W1, IR1_q, d_ff_1_q);
  D_Flip_Flop #(.trigger("rising"), .Pre_Clr_Positions("LEGACY"), .NegatePresetClear("false"), .enable("true"), .NewFFLayout("false")) d_ff_2 (
    .clk(IR2), .D(1'b1), .Q(d_ff_2_q), .reset(IR2_q));  // open: Qn, preset, en
  or or_2 (W2, IR2_q, d_ff_2_q);
  D_Flip_Flop #(.trigger("rising"), .Pre_Clr_Positions("LEGACY"), .NegatePresetClear("false"), .enable("true"), .NewFFLayout("false")) d_ff_3 (
    .clk(IR3), .D(1'b1), .Q(d_ff_3_q), .reset(IR3_q));  // open: Qn, preset, en
  or or_3 (W3, IR3_q, d_ff_3_q);
  D_Flip_Flop #(.trigger("rising"), .Pre_Clr_Positions("LEGACY"), .NegatePresetClear("false"), .enable("true"), .NewFFLayout("false")) IE (
    .clk(CLK), .D(MDin[0]), .Qn(IE_qn), .en(or_4_out), .reset(or_8_out));  // open: Q, preset
  or or_4 (or_4_out, \mcop辅助译码器_1_mtie , and_15_out);
  Hex_Digit_Display hex_digit_display_2 (.value(LedData[27:24]));  // open: dp
  Hex_Digit_Display hex_digit_display_3 (.value(LedData[23:20]));  // open: dp
  or or_5 (or_5_out, d_ff_1_q, IR1_q);
  or or_6 (or_6_out, d_ff_2_q, IR2_q);
  or or_7 (or_7_out, d_ff_3_q, IR3_q);
  or or_8 (or_8_out, \总复位 , \单周期硬布线控制器_4_三级中断_1_eret );
  Hex_Digit_Display hex_digit_display_4 (.value(LedData[15:12]));  // open: dp
  Hex_Digit_Display hex_digit_display_5 (.value(LedData[19:16]));  // open: dp
  and and_1 (and_1_out, or_5_out, ~\总复位 );  // AND_Gate
  and and_2 (and_2_out, or_6_out, ~\总复位 );  // AND_Gate
  and and_3 (and_3_out, or_7_out, ~\总复位 );  // AND_Gate
  Hex_Digit_Display hex_digit_display_6 (.value(LedData[11:8]));  // open: dp
  Hex_Digit_Display hex_digit_display_7 (.value(LedData[7:4]));  // open: dp
  // Probe on \总周期数 
  D_Flip_Flop #(.trigger("rising"), .Pre_Clr_Positions("LEGACY"), .NegatePresetClear("false"), .enable("true"), .NewFFLayout("false")) u_IR1 (
    .clk(CLK), .D(and_1_out), .Q(IR1_q), .reset(and_4_out));  // open: Qn, preset, en
  D_Flip_Flop #(.trigger("rising"), .Pre_Clr_Positions("LEGACY"), .NegatePresetClear("false"), .enable("true"), .NewFFLayout("false")) u_IR2 (
    .clk(CLK), .D(and_2_out), .Q(IR2_q), .reset(and_5_out));  // open: Qn, preset, en
  D_Flip_Flop #(.trigger("rising"), .Pre_Clr_Positions("LEGACY"), .NegatePresetClear("false"), .enable("true"), .NewFFLayout("false")) u_IR3 (
    .clk(CLK), .D(and_3_out), .Q(IR3_q), .reset(and_6_out));  // open: Qn, preset, en
  Hex_Digit_Display hex_digit_display_8 (.value(LedData[3:0]));  // open: dp
  and and_4 (and_4_out, \中断1服务中_q , and_7_out);
  and and_5 (and_5_out, \中断2服务中_q , and_9_out);
  and and_6 (and_6_out, \中断3服务中_q , \单周期硬布线控制器_4_三级中断_1_eret );
  // Probe on PC
  // Probe on IR
  or or_9 (IR1, 1'b0, 1'b0);
  D_Flip_Flop #(.trigger("rising"), .Pre_Clr_Positions("LEGACY"), .NegatePresetClear("false"), .enable("true"), .NewFFLayout("false")) \u_中断1服务中  (
    .clk(CLK), .D(IR1_q), .Q(\中断1服务中_q ), .Qn(\中断1服务中_qn ), .en(and_8_out), .reset(and_7_out));  // open: preset
  D_Flip_Flop #(.trigger("rising"), .Pre_Clr_Positions("LEGACY"), .NegatePresetClear("false"), .enable("true"), .NewFFLayout("false")) \u_中断2服务中  (
    .clk(CLK), .D(IR2_q), .Q(\中断2服务中_q ), .Qn(\中断2服务中_qn ), .en(and_10_out), .reset(and_9_out));  // open: preset
  D_Flip_Flop #(.trigger("rising"), .Pre_Clr_Positions("LEGACY"), .NegatePresetClear("false"), .enable("true"), .NewFFLayout("false")) \u_中断3服务中  (
    .clk(CLK), .D(IR3_q), .Q(\中断3服务中_q ), .Qn(\中断3服务中_qn ), .en(decoder_1_out2),
    .reset(\单周期硬布线控制器_4_三级中断_1_eret ));  // open: preset
  or or_10 (IR2, 1'b0, 1'b0);
  and and_7 (and_7_out, \单周期硬布线控制器_4_三级中断_1_eret , and_11_out);
  and and_8 (and_8_out, decoder_1_out0, and_11_out);
  and and_9 (and_9_out, \单周期硬布线控制器_4_三级中断_1_eret , \中断3服务中_qn );
  and and_10 (and_10_out, decoder_1_out1, \中断3服务中_qn );
  LED #(.active("true")) led_4 (.in(RegWrite));
  and and_11 (and_11_out, \中断2服务中_qn , \中断3服务中_qn );
  // Probe on RDin
  or or_11 (IR3, \电动机运行_电梯关门 , IRC);
  and and_12 (and_12_out, IR1_q, \中断1服务中_qn , and_11_out);
  and and_13 (and_13_out, IR2_q, \中断2服务中_qn , \中断3服务中_qn );
  and and_14 (and_14_out, IR3_q, \中断3服务中_qn );
  LED #(.active("true")) led_5 (.in(MemWrite));
  Priority_Encoder #(.select(2), .disabled("Z")) priority_encoder_1 (
    .in0(and_12_out), .in1(and_13_out), .in2(and_14_out), .in3(1'b0), .out(priority_encoder_1_out),
    .gs(priority_encoder_1_gs), .en_in(not_1_out));  // open: en_out
  not not_1 (not_1_out, 1'b0);
  // Probe on MDin
  and and_15 (and_15_out, priority_encoder_1_gs, IE_qn);
  Decoder #(.select(2), .tristate("false"), .disabled(0), .enable("true")) decoder_1 (
    .out0(decoder_1_out0), .out1(decoder_1_out1), .out2(decoder_1_out2), .sel(priority_encoder_1_out),
    .en(and_15_out));  // open: out3
  Multiplexer #(.select(2), .width(32), .disabled("Z"), .enable("false")) multiplexer_1 (
    .in0(32'hc00), .in1(32'hd40), .in2(32'he80), .in3(32'hcccccccc), .out(multiplexer_1_out),
    .sel(priority_encoder_1_out));
  Register #(.width(32), .trigger("rising"), .Select("low")) LedLock (
    .D(MDin), .en(LedNew), .Q(LedData), .clk(CLK), .clr(\总复位 ));
  or or_12 (or_12_out, \mcop辅助译码器_1_mtepc , and_15_out);
  Multiplexer #(.select(1), .width(32), .disabled("Z"), .enable("false")) multiplexer_2 (
    .in0(multiplexer_17_out), .in1(MDin), .out(multiplexer_2_out), .sel(\mcop辅助译码器_1_mtepc ));
  Multiplexer #(.select(1), .width(32), .disabled("Z"), .enable("false")) multiplexer_3 (
    .in0(multiplexer_17_out), .in1(multiplexer_1_out), .out(multiplexer_3_out), .sel(and_15_out));
  Register #(.width(32), .trigger("rising"), .Select("low")) EPC (
    .D(multiplexer_2_out), .en(or_12_out), .Q(EPC_q), .clk(CLK), .clr(\总复位 ));
  Multiplexer #(.select(1), .width(32), .disabled("Z"), .enable("false")) multiplexer_4 (
    .in0(multiplexer_3_out), .in1(EPC_q), .out(multiplexer_4_out), .sel(\单周期硬布线控制器_4_三级中断_1_eret ));
  Register #(.width(32), .trigger("rising"), .Select("low")) u_PC (
    .D(multiplexer_4_out), .en(d_ff_4_qn), .Q(PC), .clk(CLK), .clr(\总复位 ));
  Adder #(.width(32)) adder_1 (.a(PC), .b(32'h4), .out(adder_1_out), .cin(1'b0));  // open: cout
  ROM #(.addrWidth(10), .dataWidth(32), .Select("high")) rom_1 (.addr(PC[11:2]), .data(IR));
  \单周期硬布线控制器_4_三级中断  \u_单周期硬布线控制器_4_三级中断_1  (
    .OP(IR[31:26]), .Func(IR[5:0]), .ALU_OP(\单周期硬布线控制器_4_三级中断_1_alu_op ),
    .MemToReg(\单周期硬布线控制器_4_三级中断_1_memtoreg ), .MemWrite(MemWrite), .ALU_SRC(\单周期硬布线控制器_4_三级中断_1_alu_src ),
    .RegWrite(\单周期硬布线控制器_4_三级中断_1_regwrite ), .SysCALL(\单周期硬布线控制器_4_三级中断_1_syscall ), .SignedExt(SignedExt),
    .RegDst(\单周期硬布线控制器_4_三级中断_1_regdst ), .Beq(\单周期硬布线控制器_4_三级中断_1_beq ), .Bne(\单周期硬布线控制器_4_三级中断_1_bne ),
    .JR(\单周期硬布线控制器_4_三级中断_1_jr ), .JMP(\单周期硬布线控制器_4_三级中断_1_jmp ), .JAL(\单周期硬布线控制器_4_三级中断_1_jal ),
    .VarShift(VarShift), .StoreByte(LoadIn), .BGTZ(\单周期硬布线控制器_4_三级中断_1_bgtz ),
    .ERET(\单周期硬布线控制器_4_三级中断_1_eret ), .MCOP(\单周期硬布线控制器_4_三级中断_1_mcop ));
  Multiplexer #(.select(1), .width(5), .disabled("Z"), .enable("false")) multiplexer_5 (
    .in0(IR[25:21]), .in1(5'b00010), .out(multiplexer_5_out), .sel(\单周期硬布线控制器_4_三级中断_1_syscall ));
  Multiplexer #(.select(1), .width(5), .disabled("Z"), .enable("false")) multiplexer_6 (
    .in0(IR[20:16]), .in1(5'b00100), .out(multiplexer_6_out), .sel(\单周期硬布线控制器_4_三级中断_1_syscall ));
  \MCOP辅助译码器  \mcop辅助译码器_1  (
    .MCOP(\单周期硬布线控制器_4_三级中断_1_mcop ), .RS(IR[25:21]), .RD(IR[15:11]), .MFEPC(\mcop辅助译码器_1_mfepc ),
    .MTIE(\mcop辅助译码器_1_mtie ), .MTEPC(\mcop辅助译码器_1_mtepc ));
  Multiplexer #(.select(1), .width(5), .disabled("Z"), .enable("false")) multiplexer_7 (
    .in0(IR[20:16]), .in1(IR[15:11]), .out(multiplexer_7_out), .sel(\单周期硬布线控制器_4_三级中断_1_regdst ));
  Multiplexer #(.select(1), .width(32), .disabled("Z"), .enable("false")) multiplexer_8 (
    .in0(MenOut), .in1(adder_1_out), .out(multiplexer_8_out), .sel(\单周期硬布线控制器_4_三级中断_1_jal ));
  Multiplexer #(.select(1), .width(32), .disabled("Z"), .enable("false")) multiplexer_9 (
    .in0(multiplexer_8_out), .in1(EPC_q), .out(RDin), .sel(\mcop辅助译码器_1_mfepc ));
  Multiplexer #(.select(1), .width(5), .disabled("Z"), .enable("false")) multiplexer_10 (
    .in0(multiplexer_7_out), .in1({5{1'b1}}), .out(multiplexer_10_out), .sel(\单周期硬布线控制器_4_三级中断_1_jal ));
  Multiplexer #(.select(1), .width(5), .disabled("Z"), .enable("false")) multiplexer_11 (
    .in0(multiplexer_6_out), .in1({5{1'b0}}), .out(multiplexer_11_out), .sel(\单周期硬布线控制器_4_三级中断_1_bgtz ));
  or or_13 (RegWrite, \单周期硬布线控制器_4_三级中断_1_regwrite , \mcop辅助译码器_1_mfepc );
  assign bit_extender_1_out = {{16{1'b0}}, IR[15:0]};  // Bit_Extender bit_extender_1
  assign bit_extender_2_out = {{16{IR[15]}}, IR[15:0]};  // Bit_Extender bit_extender_2
  assign bit_extender_3_out = {{2{1'b0}}, IR[25:0]};  // Bit_Extender bit_extender_3
  MIPS_Regifile mips_regifile_1 (
    .Din(RDin), .Clk(CLK), .R1(mips_regifile_1_r1), .R2(MDin), .WE(RegWrite), .W_num(multiplexer_10_out),
    .R1_num(multiplexer_5_out), .R2_num(multiplexer_11_out));
  Multiplexer #(.select(1), .width(32), .disabled("Z"), .enable("false")) multiplexer_12 (
    .in0(bit_extender_1_out), .in1(bit_extender_2_out), .out(multiplexer_12_out), .sel(SignedExt));
  Multiplexer #(.select(1), .width(32), .disabled("Z"), .enable("false")) multiplexer_13 (
    .in0(MDin), .in1(multiplexer_12_out), .out(multiplexer_13_out), .sel(\单周期硬布线控制器_4_三级中断_1_alu_src ));
  and and_16 (and_16_out, not_4_out, \单周期硬布线控制器_4_三级中断_1_bgtz );
  and and_17 (and_17_out, \单周期硬布线控制器_4_三级中断_1_beq , mips_alu_1_equal);
  and and_18 (and_18_out, \单周期硬布线控制器_4_三级中断_1_bne , not_2_out);
  not not_2 (not_2_out, mips_alu_1_equal);
  and and_19 (LedNew, comparator_1_eq, \单周期硬布线控制器_4_三级中断_1_syscall );
  Comparator #(.width(32), .mode("twosComplement")) comparator_1 (
    .a(32'h22), .b(mips_regifile_1_r1), .eq(comparator_1_eq));  // open: gt, lt
  not not_3 (not_3_out, comparator_1_eq);
  Multiplexer #(.select(1), .width(5), .disabled("Z"), .enable("false")) multiplexer_14 (
    .in0(IR[10:6]), .in1(mips_regifile_1_r1[4:0]), .out(multiplexer_14_out), .sel(VarShift));
  Shifter #(.width(32), .shift("ll")) shifter_1 (.in(multiplexer_12_out), .\dist (5'b00010), .out(shifter_1_out));
  Shifter #(.width(28), .shift("ll")) shifter_2 (.in(bit_extender_3_out), .\dist (5'b00010), .out(shifter_2_out));
  or or_14 (or_14_out, and_18_out, and_17_out, and_16_out);
  and and_20 (and_20_out, \单周期硬布线控制器_4_三级中断_1_syscall , not_3_out);
  Multiplexer #(.select(1), .width(32), .disabled("Z"), .enable("false")) multiplexer_15 (
    .in0(adder_1_out), .in1(adder_2_out), .out(multiplexer_15_out), .sel(or_14_out));
  Adder #(.width(32)) adder_2 (.a(adder_1_out), .b(shifter_1_out), .out(adder_2_out), .cin(1'b0));  // open: cout
  or or_15 (or_15_out, d_ff_4_q, and_20_out);
  not not_4 (not_4_out, or_16_out);
  or or_16 (or_16_out, mips_alu_1_equal, mips_alu_1_result[0]);
  MIPS_ALU mips_alu_1 (
    .X(mips_regifile_1_r1), .Y(multiplexer_13_out), .AluOP(\单周期硬布线控制器_4_三级中断_1_alu_op ),
    .Equal(mips_alu_1_equal), .Result(mips_alu_1_result), .shamt(multiplexer_14_out));  // open: Result_2
  Multiplexer #(.select(1), .width(32), .disabled("Z"), .enable("false")) multiplexer_16 (
    .in0({PC[31:28], shifter_2_out}), .in1(mips_regifile_1_r1), .out(multiplexer_16_out),
    .sel(\单周期硬布线控制器_4_三级中断_1_jr ));
  Multiplexer #(.select(1), .width(32), .disabled("Z"), .enable("false")) multiplexer_17 (
    .in0(multiplexer_15_out), .in1(multiplexer_16_out), .out(multiplexer_17_out),
    .sel(\单周期硬布线控制器_4_三级中断_1_jmp ));
  D_Flip_Flop #(.trigger("rising"), .Pre_Clr_Positions("ABOVE_BELOW"), .NegatePresetClear("false"), .enable("false"), .NewFFLayout("true")) d_ff_4 (
    .clk(CLK), .D(or_15_out), .Q(d_ff_4_q), .Qn(d_ff_4_qn), .preset(1'b0), .reset(or_17_out));
  or or_17 (or_17_out, Go, \总复位 );
  and and_21 (and_21_out, MemWrite, d_ff_4_qn);
  Counter #(.width(16), .max('hffff), .ongoal("wrap"), .trigger("rising"), .behavior("old")) counter_1 (
    .count(d_ff_4_qn), .Q(\总周期数 ), .clk(CLK), .clr(\总复位 ));  // open: load, D, carry, preset
  RAM #(.addrWidth(10), .dataWidth(32), .bus("separate"), .Select("high")) ram_1 (
    .addr(mips_alu_1_result[11:2]), .din(MDin), .data(ram_1_data), .str(and_21_out), .clk(CLK), .clr(\总复位 ));  // open: sel, ld
  Multiplexer #(.select(1), .width(32), .disabled("Z"), .enable("false")) multiplexer_18 (
    .in0(mips_alu_1_result), .in1(ram_1_data), .out(multiplexer_18_out), .sel(\单周期硬布线控制器_4_三级中断_1_memtoreg ));
  Multiplexer #(.select(1), .width(32), .disabled("Z"), .enable("false")) multiplexer_19 (
    .in0(multiplexer_18_out), .in1(multiplexer_20_out), .out(MenOut), .sel(LoadIn));
  Multiplexer #(.select(2), .width(32), .disabled("Z"), .enable("false")) multiplexer_20 (
    .in0(\输入数据0_向上 ), .in1(\输入数据1_向下 ), .in2(\输入数据2_内部 ), .in3(\输入数据3_当前楼层 ), .out(multiplexer_20_out),
    .sel(IR[22:21]));

  // Other names for the same wires on the sheet: IR_RS[4:0] = IR[25:21]; RBOut[31:0] = MDin; RST = \总复位 

  // Notes on the sheet:
  //   中断源
  //   中断等待指示
  //   总复位信号应将除ROM以外所有存储组件全部清零
  //   数码管输出
  //   数码管输出应该用寄存器锁存，否则显示数据只能一闪而过
  //   Reset 
  //   Reset 
  //   Reset 
  //   为方便自动评测，需要输出PC，IR，寄存器堆写如数据RDin
  //   RAM写使能MemWrite、RAM写入数据MDin等信号
  //   指令字
  //   contents of rom_1 (hex, n*v repeats v):
  //   20100001 40906000 201e0ffc 201d0ffc 40806000 20100001 40906000 1008020 1208820 1409020 1609820
  //   40806000 b020 2d0b025 2d1b025 2d2b025 12c00022 20180001 2279ffff 338c004 12d8001e 20010002 1034000c
  //   20140001 200a820 275a806 1ea00019 220a820 275a806 1ea00016 240a820 275a806 1ea00013 20140002
  //   10000011 20160021 2d3b822 200a820 2f5a804 2f5a806 1ea0000b 220a820 2f5a804 2f5a806 1ea00007 240a820
  //   2f5a804 2f5a806 1ea00003 20140001 10000001 a020 142020 20020022 c 1020 1000ffcc c 710*0 a0080000
  //   a0290000 a04a0000 a06b0000 42000018 75*0 a0080000 a0290000 a04a0000 a06b0000 42000018 75*0 a0080000
  //   a0290000 a04a0000 a06b0000 42000018
  //   ERET
  //   JMP
  //   JR
  //   OP
  //   OP
  //   Func
  //   Func
  //   rs
  //   rt
  //   rd
  //   shmat
  //   Imm16
  //   Imm26
  //   High4
  //   MCOP
  //   BGTZ
  //   Beq
  //   Bne
  //   MemToReg
  //   MemWrite
  //   AluOP
  //   AluSrcB
  //   RegWrite
  //   JAL
  //   RegDst
  //   Syscall
  //   MCOP辅助译码器
endmodule

// 单周期硬布线控制器
module \单周期硬布线控制器_4_三级中断  (
  input  [5:0] OP,
  input  [5:0] Func,
  output [3:0] ALU_OP,
  output MemToReg,
  output MemWrite,
  output ALU_SRC,
  output RegWrite,
  output SysCALL,
  output SignedExt,
  output RegDst,
  output Beq,
  output Bne,
  output JR,
  output JMP,
  output JAL,
  output VarShift,
  output StoreByte,
  output BGTZ,
  output ERET,
  output MCOP
);

  \运算控制器自动生成_4_三级中断  \u_运算控制器自动生成_4_三级中断_1  (
    .OP0(OP[0]), .OP1(OP[1]), .OP2(OP[2]), .OP3(OP[3]), .OP4(OP[4]), .OP5(OP[5]), .F0(Func[0]), .F1(Func[1]),
    .F2(Func[2]), .F3(Func[3]), .F4(Func[4]), .F5(Func[5]), .S0(ALU_OP[0]), .S1(ALU_OP[1]), .S2(ALU_OP[2]),
    .S3(ALU_OP[3]));
  \控制信号自动生成_4_三级中断  \u_控制信号自动生成_4_三级中断_1  (
    .OP0(OP[0]), .OP1(OP[1]), .OP2(OP[2]), .OP3(OP[3]), .OP4(OP[4]), .OP5(OP[5]), .F0(Func[0]), .F1(Func[1]),
    .F2(Func[2]), .F3(Func[3]), .F4(Func[4]), .F5(Func[5]), .MemToReg(MemToReg), .MemWrite(MemWrite),
    .ALU_SRC(ALU_SRC), .RegWrite(RegWrite), .SysCALL(SysCALL), .SignedExt(SignedExt), .RegDst(RegDst),
    .BEQ(Beq), .BNE(Bne), .JR(JR), .JUMP(JMP), .JAL(JAL));
  \扩展_控制信号自动生成_4_三级中断  \u_扩展_控制信号自动生成_4_三级中断_1  (
    .OP0(OP[0]), .OP1(OP[1]), .OP2(OP[2]), .OP3(OP[3]), .OP4(OP[4]), .OP5(OP[5]), .F0(Func[0]),
    .VarShift(VarShift), .F1(Func[1]), .F2(Func[2]), .F3(Func[3]), .F4(Func[4]), .F5(Func[5]),
    .StoreByte(StoreByte), .BGTZ(BGTZ), .ERET(ERET), .MFC0(MCOP));

  // Other names for the same wires on the sheet: OP_CODE[5:0] = OP

  // Notes on the sheet:
  //   控制信号生成，产生数据通路需要的其他控制信号
  //   Logisim软件一次只能自动生成12个输出信号，故需要分开
  //   运算器控制器，根据指令生成运算器功能选择信号
endmodule

// 运算器控制器
module \运算控制器自动生成_4_三级中断  (
  input  OP0,
  input  OP1,
  input  OP2,
  input  OP3,
  input  OP4,
  input  OP5,
  input  F0,
  input  F1,
  input  F2,
  input  F3,
  input  F4,
  input  F5,
  output S0,
  output S1,
  output S2,
  output S3
);

  wire and_1_out, and_2_out, and_3_out, and_4_out, and_5_out, and_6_out, and_7_out, and_8_out, and_9_out,
       and_10_out, and_11_out, and_12_out, and_13_out, and_14_out, and_15_out, and_16_out, and_17_out,
       and_18_out, and_19_out, and_20_out, and_21_out, and_22_out, and_23_out, and_24_out, and_25_out,
       and_26_out, and_27_out, and_28_out, and_29_out, and_30_out, and_31_out, and_32_out, and_33_out,
       and_34_out, and_35_out, and_36_out, and_37_out, and_38_out, and_39_out, and_40_out, and_41_out,
       and_42_out, and_43_out, and_44_out, not_1_out, not_2_out, not_3_out, not_4_out, not_5_out, not_6_out,
       not_7_out, not_8_out, not_9_out, not_10_out, not_11_out, not_12_out, not_13_out, not_14_out,
       not_15_out, not_16_out, not_17_out, not_18_out, not_19_out, not_20_out, not_21_out, not_22_out,
       not_23_out, not_24_out, not_25_out, not_26_out, not_27_out, not_28_out, not_29_out, not_30_out,
       not_31_out, not_32_out, not_33_out, not_34_out, not_35_out, not_36_out, not_37_out, not_38_out,
       not_39_out, not_40_out, not_41_out, not_42_out, not_43_out, not_44_out, not_45_out, not_46_out,
       not_47_out, not_48_out, not_49_out, not_50_out, not_51_out, not_52_out, not_53_out, not_54_out,
       not_55_out, not_56_out, not_57_out, not_58_out, not_59_out, not_60_out, not_61_out, not_62_out,
       not_63_out, not_64_out, not_65_out, not_66_out, not_67_out, not_68_out, not_69_out, not_70_out,
       not_71_out, not_72_out, not_73_out, not_74_out, not_75_out, not_76_out, not_77_out, not_78_out,
       not_79_out, not_80_out, not_81_out, not_82_out, not_83_out, not_84_out, not_85_out, not_86_out,
       not_87_out, not_88_out, not_89_out, not_90_out, not_91_out, not_92_out, not_93_out, not_94_out,
       not_95_out, not_96_out, not_97_out, not_98_out, not_99_out, not_100_out, not_101_out, not_102_out,
       not_103_out, not_104_out, not_105_out, not_106_out, not_107_out, not_108_out, not_109_out,
       not_110_out, not_111_out, not_112_out, not_113_out, not_114_out, not_115_out, not_116_out,
       not_117_out, not_118_out, not_119_out, not_120_out, not_121_out, not_122_out, not_123_out,
       not_124_out, not_125_out, not_126_out, not_127_out, not_128_out, not_129_out, not_130_out,
       not_131_out, not_132_out, not_133_out, not_134_out, not_135_out, not_136_out, not_137_out,
       not_138_out, not_139_out, not_140_out, not_141_out, not_142_out, not_143_out, not_144_out,
       not_145_out, not_146_out, not_147_out, not_148_out, not_149_out, not_150_out, not_151_out,
       not_152_out, not_153_out, not_154_out, not_155_out, not_156_out, not_157_out, not_158_out,
       not_159_out, not_160_out, not_161_out, not_162_out, not_163_out, not_164_out, not_165_out,
       not_166_out, not_167_out, not_168_out, not_169_out, not_170_out, not_171_out, not_172_out,
       not_173_out, not_174_out, not_175_out, not_176_out, not_177_out, not_178_out, not_179_out,
       not_180_out, not_181_out, not_182_out, not_183_out, not_184_out, not_185_out, not_186_out,
       not_187_out, not_188_out, not_189_out, not_190_out, not_191_out, not_192_out, not_193_out,
       not_194_out, not_195_out, not_196_out, not_197_out, not_198_out, not_199_out, not_200_out,
       not_201_out, not_202_out, not_203_out, not_204_out, not_205_out, not_206_out, not_207_out,
       not_208_out, not_209_out, not_210_out, not_211_out, not_212_out, not_213_out, not_214_out,
       not_215_out, not_216_out, not_217_out, not_218_out, not_219_out, not_220_out, not_221_out,
       not_222_out, not_223_out, not_224_out, not_225_out, not_226_out, not_227_out, not_228_out,
       not_229_out, not_230_out, not_231_out, not_232_out, not_233_out, not_234_out, not_235_out,
       not_236_out, not_237_out, not_238_out, not_239_out, not_240_out, not_241_out, not_242_out,
       not_243_out, not_244_out, not_245_out, not_246_out, not_247_out, not_248_out, not_249_out,
       not_250_out, not_251_out, not_252_out, not_253_out, not_254_out, not_255_out, not_256_out,
       not_257_out, not_258_out, not_259_out, not_260_out, not_261_out, not_262_out, not_263_out,
       not_264_out, not_265_out, not_266_out, not_267_out, not_268_out, not_269_out, not_270_out,
       not_271_out, not_272_out, not_273_out, not_274_out, not_275_out, not_276_out, not_277_out,
       not_278_out, not_279_out, not_280_out, not_281_out;

  not not_1 (not_1_out, OP5);
  not not_2 (not_2_out, OP4);
  not not_3 (not_3_out, OP3);
  not not_4 (not_4_out, OP2);
  not not_5 (not_5_out, OP1);
  not not_6 (not_6_out, OP0);
  not not_7 (not_7_out, F5);
  not not_8 (not_8_out, F4);
  not not_9 (not_9_out, F3);
  not not_10 (not_10_out, F2);
  not not_11 (not_11_out, OP5);
  not not_12 (not_12_out, OP4);
  not not_13 (not_13_out, OP3);
  not not_14 (not_14_out, OP2);
  not not_15 (not_15_out, OP1);
  not not_16 (not_16_out, OP0);
  not not_17 (not_17_out, F4);
  not not_18 (not_18_out, F3);
  not not_19 (not_19_out, F2);
  not not_20 (not_20_out, F1);
  not not_21 (not_21_out, F0);
  not not_22 (not_22_out, OP5);
  not not_23 (not_23_out, OP4);
  not not_24 (not_24_out, OP3);
  not not_25 (not_25_out, OP2);
  not not_26 (not_26_out, OP1);
  not not_27 (not_27_out, OP0);
  not not_28 (not_28_out, F4);
  not not_29 (not_29_out, F3);
  not not_30 (not_30_out, F2);
  not not_31 (not_31_out, F1);
  not not_32 (not_32_out, OP5);
  not not_33 (not_33_out, OP4);
  not not_34 (not_34_out, OP3);
  not not_35 (not_35_out, OP2);
  not not_36 (not_36_out, OP1);
  not not_37 (not_37_out, OP0);
  not not_38 (not_38_out, F4);
  not not_39 (not_39_out, F3);
  not not_40 (not_40_out, F1);
  not not_41 (not_41_out, F0);
  not not_42 (not_42_out, OP5);
  not not_43 (not_43_out, OP4);
  not not_44 (not_44_out, OP3);
  not not_45 (not_45_out, OP2);
  not not_46 (not_46_out, OP1);
  not not_47 (not_47_out, OP0);
  not not_48 (not_48_out, F4);
  not not_49 (not_49_out, F2);
  not not_50 (not_50_out, F0);
  not not_51 (not_51_out, OP5);
  not not_52 (not_52_out, OP4);
  not not_53 (not_53_out, OP2);
  not not_54 (not_54_out, OP1);
  not not_55 (not_55_out, OP0);
  not not_56 (not_56_out, OP5);
  not not_57 (not_57_out, OP4);
  not not_58 (not_58_out, OP1);
  not not_59 (not_59_out, OP0);
  not not_60 (not_60_out, OP5);
  not not_61 (not_61_out, OP4);
  not not_62 (not_62_out, OP2);
  not not_63 (not_63_out, OP1);
  not not_64 (not_64_out, OP5);
  not not_65 (not_65_out, OP4);
  not not_66 (not_66_out, OP2);
  not not_67 (not_67_out, OP0);
  not not_68 (not_68_out, OP4);
  not not_69 (not_69_out, OP3);
  not not_70 (not_70_out, OP2);
  not not_71 (not_71_out, OP4);
  not not_72 (not_72_out, OP2);
  not not_73 (not_73_out, OP4);
  not not_74 (not_74_out, OP2);
  not not_75 (not_75_out, OP1);
  not not_76 (not_76_out, OP0);
  not not_77 (not_77_out, OP5);
  not not_78 (not_78_out, OP4);
  not not_79 (not_79_out, OP3);
  not not_80 (not_80_out, OP5);
  not not_81 (not_81_out, OP4);
  not not_82 (not_82_out, OP3);
  not not_83 (not_83_out, OP2);
  not not_84 (not_84_out, OP1);
  not not_85 (not_85_out, OP0);
  not not_86 (not_86_out, F5);
  not not_87 (not_87_out, F4);
  not not_88 (not_88_out, F3);
  not not_89 (not_89_out, F2);
  not not_90 (not_90_out, F0);
  not not_91 (not_91_out, OP5);
  not not_92 (not_92_out, OP4);
  not not_93 (not_93_out, OP3);
  not not_94 (not_94_out, OP2);
  not not_95 (not_95_out, OP1);
  not not_96 (not_96_out, OP0);
  not not_97 (not_97_out, F4);
  not not_98 (not_98_out, F3);
  not not_99 (not_99_out, F2);
  not not_100 (not_100_out, F0);
  not not_101 (not_101_out, OP5);
  not not_102 (not_102_out, OP4);
  not not_103 (not_103_out, OP3);
  not not_104 (not_104_out, OP2);
  not not_105 (not_105_out, OP1);
  not not_106 (not_106_out, OP0);
  not not_107 (not_107_out, F4);
  not not_108 (not_108_out, F3);
  not not_109 (not_109_out, F1);
  not not_110 (not_110_out, F0);
  not not_111 (not_111_out, OP5);
  not not_112 (not_112_out, OP4);
  not not_113 (not_113_out, OP3);
  not not_114 (not_114_out, OP2);
  not not_115 (not_115_out, OP1);
  not not_116 (not_116_out, OP0);
  not not_117 (not_117_out, F4);
  not not_118 (not_118_out, F3);
  not not_119 (not_119_out, OP5);
  not not_120 (not_120_out, OP4);
  not not_121 (not_121_out, OP3);
  not not_122 (not_122_out, OP2);
  not not_123 (not_123_out, OP1);
  not not_124 (not_124_out, OP0);
  not not_125 (not_125_out, F4);
  not not_126 (not_126_out, F2);
  not not_127 (not_127_out, F0);
  not not_128 (not_128_out, OP5);
  not not_129 (not_129_out, OP4);
  not not_130 (not_130_out, OP1);
  not not_131 (not_131_out, OP0);
  not not_132 (not_132_out, OP5);
  not not_133 (not_133_out, OP4);
  not not_134 (not_134_out, OP2);
  not not_135 (not_135_out, OP0);
  not not_136 (not_136_out, OP5);
  not not_137 (not_137_out, OP4);
  not not_138 (not_138_out, OP3);
  not not_139 (not_139_out, OP2);
  not not_140 (not_140_out, OP1);
  not not_141 (not_141_out, OP0);
  not not_142 (not_142_out, F5);
  not not_143 (not_143_out, F4);
  not not_144 (not_144_out, F3);
  not not_145 (not_145_out, F0);
  not not_146 (not_146_out, OP5);
  not not_147 (not_147_out, OP4);
  not not_148 (not_148_out, OP3);
  not not_149 (not_149_out, OP5);
  not not_150 (not_150_out, OP4);
  not not_151 (not_151_out, OP3);
  not not_152 (not_152_out, OP2);
  not not_153 (not_153_out, OP1);
  not not_154 (not_154_out, OP0);
  not not_155 (not_155_out, F4);
  not not_156 (not_156_out, F3);
  not not_157 (not_157_out, F2);
  not not_158 (not_158_out, F1);
  not not_159 (not_159_out, F0);
  not not_160 (not_160_out, OP5);
  not not_161 (not_161_out, OP4);
  not not_162 (not_162_out, OP3);
  not not_163 (not_163_out, OP2);
  not not_164 (not_164_out, OP1);
  not not_165 (not_165_out, OP0);
  not not_166 (not_166_out, F4);
  not not_167 (not_167_out, F3);
  not not_168 (not_168_out, F2);
  not not_169 (not_169_out, F1);
  not not_170 (not_170_out, OP5);
  not not_171 (not_171_out, OP4);
  not not_172 (not_172_out, OP3);
  not not_173 (not_173_out, OP2);
  not not_174 (not_174_out, OP1);
  not not_175 (not_175_out, OP0);
  not not_176 (not_176_out, F4);
  not not_177 (not_177_out, F3);
  not not_178 (not_178_out, F2);
  not not_179 (not_179_out, F0);
  not not_180 (not_180_out, OP5);
  not not_181 (not_181_out, OP4);
  not not_182 (not_182_out, OP3);
  not not_183 (not_183_out, OP2);
  not not_184 (not_184_out, OP1);
  not not_185 (not_185_out, OP0);
  not not_186 (not_186_out, F4);
  not not_187 (not_187_out, F3);
  not not_188 (not_188_out, F1);
  not not_189 (not_189_out, F0);
  not not_190 (not_190_out, OP5);
  not not_191 (not_191_out, OP4);
  not not_192 (not_192_out, OP3);
  not not_193 (not_193_out, OP2);
  not not_194 (not_194_out, OP1);
  not not_195 (not_195_out, OP0);
  not not_196 (not_196_out, F4);
  not not_197 (not_197_out, F2);
  not not_198 (not_198_out, OP5);
  not not_199 (not_199_out, OP4);
  not not_200 (not_200_out, OP3);
  not not_201 (not_201_out, OP1);
  not not_202 (not_202_out, OP0);
  not not_203 (not_203_out, OP5);
  not not_204 (not_204_out, OP4);
  not not_205 (not_205_out, OP3);
  not not_206 (not_206_out, OP1);
  not not_207 (not_207_out, OP5);
  not not_208 (not_208_out, OP4);
  not not_209 (not_209_out, OP2);
  not not_210 (not_210_out, OP1);
  not not_211 (not_211_out, OP0);
  not not_212 (not_212_out, OP5);
  not not_213 (not_213_out, OP4);
  not not_214 (not_214_out, OP1);
  not not_215 (not_215_out, OP0);
  not not_216 (not_216_out, OP5);
  not not_217 (not_217_out, OP4);
  not not_218 (not_218_out, OP2);
  not not_219 (not_219_out, OP1);
  not not_220 (not_220_out, OP4);
  not not_221 (not_221_out, OP3);
  not not_222 (not_222_out, OP2);
  not not_223 (not_223_out, OP4);
  not not_224 (not_224_out, OP2);
  not not_225 (not_225_out, OP4);
  not not_226 (not_226_out, OP2);
  not not_227 (not_227_out, OP1);
  not not_228 (not_228_out, OP0);
  not not_229 (not_229_out, OP5);
  not not_230 (not_230_out, OP4);
  not not_231 (not_231_out, OP3);
  not not_232 (not_232_out, OP2);
  not not_233 (not_233_out, OP1);
  not not_234 (not_234_out, OP0);
  not not_235 (not_235_out, F4);
  not not_236 (not_236_out, F3);
  not not_237 (not_237_out, F1);
  not not_238 (not_238_out, OP5);
  not not_239 (not_239_out, OP4);
  not not_240 (not_240_out, OP3);
  not not_241 (not_241_out, OP2);
  not not_242 (not_242_out, OP1);
  not not_243 (not_243_out, OP0);
  not not_244 (not_244_out, F4);
  not not_245 (not_245_out, F3);
  not not_246 (not_246_out, OP5);
  not not_247 (not_247_out, OP4);
  not not_248 (not_248_out, OP3);
  not not_249 (not_249_out, OP2);
  not not_250 (not_250_out, OP1);
  not not_251 (not_251_out, OP0);
  not not_252 (not_252_out, F4);
  not not_253 (not_253_out, F2);
  not not_254 (not_254_out, F0);
  not not_255 (not_255_out, OP5);
  not not_256 (not_256_out, OP4);
  not not_257 (not_257_out, OP3);
  not not_258 (not_258_out, OP2);
  not not_259 (not_259_out, OP1);
  not not_260 (not_260_out, OP0);
  not not_261 (not_261_out, F4);
  not not_262 (not_262_out, F2);
  not not_263 (not_263_out, OP5);
  not not_264 (not_264_out, OP4);
  not not_265 (not_265_out, OP3);
  not not_266 (not_266_out, OP1);
  not not_267 (not_267_out, OP0);
  not not_268 (not_268_out, OP5);
  not not_269 (not_269_out, OP4);
  not not_270 (not_270_out, OP3);
  not not_271 (not_271_out, OP1);
  not not_272 (not_272_out, OP5);
  not not_273 (not_273_out, OP4);
  not not_274 (not_274_out, OP2);
  not not_275 (not_275_out, OP0);
  not not_276 (not_276_out, OP5);
  not not_277 (not_277_out, OP4);
  not not_278 (not_278_out, OP1);
  not not_279 (not_279_out, OP5);
  not not_280 (not_280_out, OP4);
  not not_281 (not_281_out, OP3);
  and and_1 (and_1_out, not_1_out, not_2_out, not_3_out, not_4_out, not_5_out, not_6_out, not_7_out, not_8_out, not_9_out, not_10_out, F1, F0);
  and and_2 (and_2_out, not_11_out, not_12_out, not_13_out, not_14_out, not_15_out, not_16_out, F5, not_17_out, not_18_out, not_19_out, not_20_out, not_21_out);
  and and_3 (and_3_out, not_22_out, not_23_out, not_24_out, not_25_out, not_26_out, not_27_out, F5, not_28_out, not_29_out, not_30_out, not_31_out, F0);
  and and_4 (and_4_out, not_32_out, not_33_out, not_34_out, not_35_out, not_36_out, not_37_out, F5, not_38_out, not_39_out, F2, not_40_out, not_41_out);
  and and_5 (and_5_out, not_42_out, not_43_out, not_44_out, not_45_out, not_46_out, not_47_out, F5, not_48_out, F3, not_49_out, F1, not_50_out);
  and and_6 (and_6_out, not_51_out, not_52_out, OP3, not_53_out, not_54_out, not_55_out);
  and and_7 (and_7_out, not_56_out, not_57_out, OP3, OP2, not_58_out, not_59_out);
  and and_8 (and_8_out, not_60_out, not_61_out, OP3, not_62_out, not_63_out, OP0);
  and and_9 (and_9_out, not_64_out, not_65_out, OP3, not_66_out, OP1, not_67_out);
  and and_10 (and_10_out, OP5, not_68_out, not_69_out, not_70_out, OP1, OP0);
  and and_11 (and_11_out, OP5, not_71_out, OP3, not_72_out, OP1, OP0);
  and and_12 (and_12_out, OP5, not_73_out, OP3, not_74_out, not_75_out, not_76_out);
  and and_13 (and_13_out, not_77_out, not_78_out, not_79_out, OP2, OP1, OP0);
  and and_14 (and_14_out, not_80_out, not_81_out, not_82_out, not_83_out, not_84_out, not_85_out, not_86_out, not_87_out, not_88_out, not_89_out, F1, not_90_out);
  and and_15 (and_15_out, not_91_out, not_92_out, not_93_out, not_94_out, not_95_out, not_96_out, F5, not_97_out, not_98_out, not_99_out, F1, not_100_out);
  and and_16 (and_16_out, not_101_out, not_102_out, not_103_out, not_104_out, not_105_out, not_106_out, F5, not_107_out, not_108_out, F2, not_109_out, not_110_out);
  and and_17 (and_17_out, not_111_out, not_112_out, not_113_out, not_114_out, not_115_out, not_116_out, F5, not_117_out, not_118_out, F2, F1, F0);
  and and_18 (and_18_out, not_119_out, not_120_out, not_121_out, not_122_out, not_123_out, not_124_out, F5, not_125_out, F3, not_126_out, F1, not_127_out);
  and and_19 (and_19_out, not_128_out, not_129_out, OP3, OP2, not_130_out, not_131_out);
  and and_20 (and_20_out, not_132_out, not_133_out, OP3, not_134_out, OP1, not_135_out);
  and and_21 (and_21_out, not_136_out, not_137_out, not_138_out, not_139_out, not_140_out, not_141_out, not_142_out, not_143_out, not_144_out, F2, F1, not_145_out);
  and and_22 (and_22_out, not_146_out, not_147_out, not_148_out, OP2, OP1, OP0);
  and and_23 (and_23_out, not_149_out, not_150_out, not_151_out, not_152_out, not_153_out, not_154_out, F5, not_155_out, not_156_out, not_157_out, not_158_out, not_159_out);
  and and_24 (and_24_out, not_160_out, not_161_out, not_162_out, not_163_out, not_164_out, not_165_out, F5, not_166_out, not_167_out, not_168_out, not_169_out, F0);
  and and_25 (and_25_out, not_170_out, not_171_out, not_172_out, not_173_out, not_174_out, not_175_out, F5, not_176_out, not_177_out, not_178_out, F1, not_179_out);
  and and_26 (and_26_out, not_180_out, not_181_out, not_182_out, not_183_out, not_184_out, not_185_out, F5, not_186_out, not_187_out, F2, not_188_out, not_189_out);
  and and_27 (and_27_out, not_190_out, not_191_out, not_192_out, not_193_out, not_194_out, not_195_out, F5, not_196_out, F3, not_197_out, F1, F0);
  and and_28 (and_28_out, not_198_out, not_199_out, not_200_out, OP2, not_201_out, not_202_out);
  and and_29 (and_29_out, not_203_out, not_204_out, not_205_out, OP2, not_206_out, OP0);
  and and_30 (and_30_out, not_207_out, not_208_out, OP3, not_209_out, not_210_out, not_211_out);
  and and_31 (and_31_out, not_212_out, not_213_out, OP3, OP2, not_214_out, not_215_out);
  and and_32 (and_32_out, not_216_out, not_217_out, OP3, not_218_out, not_219_out, OP0);
  and and_33 (and_33_out, OP5, not_220_out, not_221_out, not_222_out, OP1, OP0);
  and and_34 (and_34_out, OP5, not_223_out, OP3, not_224_out, OP1, OP0);
  and and_35 (and_35_out, OP5, not_225_out, OP3, not_226_out, not_227_out, not_228_out);
  and and_36 (and_36_out, not_229_out, not_230_out, not_231_out, not_232_out, not_233_out, not_234_out, F5, not_235_out, not_236_out, F2, not_237_out, F0);
  and and_37 (and_37_out, not_238_out, not_239_out, not_240_out, not_241_out, not_242_out, not_243_out, F5, not_244_out, not_245_out, F2, F1, F0);
  and and_38 (and_38_out, not_246_out, not_247_out, not_248_out, not_249_out, not_250_out, not_251_out, F5, not_252_out, F3, not_253_out, F1, not_254_out);
  and and_39 (and_39_out, not_255_out, not_256_out, not_257_out, not_258_out, not_259_out, not_260_out, F5, not_261_out, F3, not_262_out, F1, F0);
  and and_40 (and_40_out, not_263_out, not_264_out, not_265_out, OP2, not_266_out, not_267_out);
  and and_41 (and_41_out, not_268_out, not_269_out, not_270_out, OP2, not_271_out, OP0);
  and and_42 (and_42_out, not_272_out, not_273_out, OP3, not_274_out, OP1, not_275_out);
  and and_43 (and_43_out, not_276_out, not_277_out, OP3, OP2, not_278_out, OP0);
  and and_44 (and_44_out, not_279_out, not_280_out, not_281_out, OP2, OP1, OP0);
  or or_1 (S1, and_14_out, and_15_out, and_16_out, and_17_out, and_18_out, and_19_out, and_20_out, and_21_out, and_22_out);
  or or_2 (S3, and_36_out, and_37_out, and_38_out, and_39_out, and_40_out, and_41_out, and_42_out, and_43_out, and_44_out);
  or or_3 (S0, and_1_out, and_2_out, and_3_out, and_4_out, and_5_out, and_6_out, and_7_out, and_8_out, and_9_out, and_10_out, and_11_out, and_12_out, and_13_out);
  or or_4 (S2, and_23_out, and_24_out, and_25_out, and_26_out, and_27_out, and_28_out, and_29_out, and_30_out, and_31_out, and_32_out, and_33_out, and_34_out, and_35_out);
endmodule
// 控制信号生成
module \控制信号自动生成_4_三级中断  (
  input  OP0,
  input  OP1,
  input  OP2,
  input  OP3,
  input  OP4,
  input  OP5,
  input  F0,
  input  F1,
  input  F2,
  input  F3,
  input  F4,
  input  F5,
  output MemToReg,
  output MemWrite,
  output ALU_SRC,
  output RegWrite,
  output SysCALL,
  output SignedExt,
  output RegDst,
  output BEQ,
  output BNE,
  output JR,
  output JUMP,
  output JAL
);

  wire and_3_out, and_4_out, and_5_out, and_6_out, and_7_out, and_8_out, and_9_out, and_10_out, and_11_out,
       and_12_out, and_13_out, and_14_out, and_15_out, and_16_out, and_17_out, and_18_out, and_19_out,
       and_20_out, and_21_out, and_22_out, and_23_out, and_24_out, and_25_out, and_26_out, and_27_out,
       and_28_out, and_29_out, and_30_out, and_32_out, and_33_out, and_34_out, and_35_out, and_36_out,
       and_37_out, and_38_out, and_39_out, and_40_out, and_41_out, and_42_out, and_43_out, and_44_out,
       and_45_out, and_46_out, and_47_out, and_48_out, and_49_out, and_50_out, and_51_out, and_52_out,
       and_53_out, and_57_out, and_58_out, and_59_out, not_1_out, not_2_out, not_3_out, not_4_out, not_5_out,
       not_6_out, not_7_out, not_8_out, not_9_out, not_10_out, not_11_out, not_12_out, not_13_out,
       not_14_out, not_15_out, not_16_out, not_17_out, not_18_out, not_19_out, not_20_out, not_21_out,
       not_22_out, not_23_out, not_24_out, not_25_out, not_26_out, not_27_out, not_28_out, not_29_out,
       not_30_out, not_31_out, not_32_out, not_33_out, not_34_out, not_35_out, not_36_out, not_37_out,
       not_38_out, not_39_out, not_40_out, not_41_out, not_42_out, not_43_out, not_44_out, not_45_out,
       not_46_out, not_47_out, not_48_out, not_49_out, not_50_out, not_51_out, not_52_out, not_53_out,
       not_54_out, not_55_out, not_56_out, not_57_out, not_58_out, not_59_out, not_60_out, not_61_out,
       not_62_out, not_63_out, not_64_out, not_65_out, not_66_out, not_67_out, not_68_out, not_69_out,
       not_70_out, not_71_out, not_72_out, not_73_out, not_74_out, not_75_out, not_76_out, not_77_out,
       not_78_out, not_79_out, not_80_out, not_81_out, not_82_out, not_83_out, not_84_out, not_85_out,
       not_86_out, not_87_out, not_88_out, not_89_out, not_90_out, not_91_out, not_92_out, not_93_out,
       not_94_out, not_95_out, not_96_out, not_97_out, not_98_out, not_99_out, not_100_out, not_101_out,
       not_102_out, not_103_out, not_104_out, not_105_out, not_106_out, not_107_out, not_108_out,
       not_109_out, not_110_out, not_111_out, not_112_out, not_113_out, not_114_out, not_115_out,
       not_116_out, not_117_out, not_118_out, not_119_out, not_120_out, not_121_out, not_122_out,
       not_123_out, not_124_out, not_125_out, not_126_out, not_127_out, not_128_out, not_129_out,
       not_130_out, not_131_out, not_132_out, not_133_out, not_134_out, not_135_out, not_136_out,
       not_137_out, not_138_out, not_139_out, not_140_out, not_141_out, not_142_out, not_143_out,
       not_144_out, not_145_out, not_146_out, not_147_out, not_148_out, not_149_out, not_150_out,
       not_151_out, not_152_out, not_153_out, not_154_out, not_155_out, not_156_out, not_157_out,
       not_158_out, not_159_out, not_160_out, not_161_out, not_162_out, not_163_out, not_164_out,
       not_165_out, not_166_out, not_167_out, not_168_out, not_169_out, not_170_out, not_171_out,
       not_172_out, not_173_out, not_174_out, not_175_out, not_176_out, not_177_out, not_178_out,
       not_179_out, not_180_out, not_181_out, not_182_out, not_183_out, not_184_out, not_185_out,
       not_186_out, not_187_out, not_188_out, not_189_out, not_190_out, not_191_out, not_192_out,
       not_193_out, not_194_out, not_195_out, not_196_out, not_197_out, not_198_out, not_199_out,
       not_200_out, not_201_out, not_202_out, not_203_out, not_204_out, not_205_out, not_206_out,
       not_207_out, not_208_out, not_209_out, not_210_out, not_211_out, not_212_out, not_213_out,
       not_214_out, not_215_out, not_216_out, not_217_out, not_218_out, not_219_out, not_220_out,
       not_221_out, not_222_out, not_223_out, not_224_out, not_225_out, not_226_out, not_227_out,
       not_228_out, not_229_out, not_230_out, not_231_out, not_232_out, not_233_out, not_234_out,
       not_235_out, not_236_out, not_237_out, not_238_out, not_239_out, not_240_out, not_241_out,
       not_242_out, not_243_out, not_244_out, not_245_out, not_246_out, not_247_out, not_248_out,
       not_249_out, not_250_out, not_251_out, not_252_out, not_253_out, not_254_out, not_255_out,
       not_256_out, not_257_out, not_258_out, not_259_out, not_260_out, not_261_out, not_262_out,
       not_263_out, not_264_out, not_265_out, not_266_out, not_267_out, not_268_out, not_269_out,
       not_270_out, not_271_out, not_272_out, not_273_out, not_274_out, not_275_out, not_276_out,
       not_277_out, not_278_out, not_279_out, not_280_out, not_281_out, not_282_out, not_283_out,
       not_284_out, not_285_out, not_286_out, not_287_out, not_288_out, not_289_out, not_290_out,
       not_291_out, not_292_out, not_293_out, not_294_out, not_295_out, not_296_out, not_297_out,
       not_298_out, not_299_out, not_300_out, not_301_out, not_302_out, not_303_out, not_304_out,
       not_305_out, not_306_out, not_307_out, not_308_out, not_309_out, not_310_out, not_311_out,
       not_312_out, not_313_out, not_314_out, not_315_out, not_316_out, not_317_out, not_318_out,
       not_319_out, not_320_out, not_321_out, not_322_out, not_323_out, not_324_out, not_325_out,
       not_326_out, not_327_out, not_328_out, not_329_out, not_330_out, not_331_out, not_332_out,
       not_333_out, not_334_out, not_335_out, not_336_out, not_337_out, not_338_out, not_339_out,
       not_340_out, not_341_out, not_342_out, not_343_out, not_344_out, not_345_out, not_346_out,
       not_347_out, not_348_out, not_349_out, not_350_out, not_351_out, not_352_out, not_353_out,
       not_354_out, not_355_out, not_356_out, not_357_out, not_358_out, not_359_out, not_360_out,
       not_361_out, not_362_out, not_363_out, not_364_out, not_365_out, not_366_out, not_367_out,
       not_368_out, not_369_out, not_370_out, not_371_out, not_372_out, not_373_out, not_374_out,
       not_375_out, not_376_out, not_377_out, not_378_out, not_379_out, not_380_out, not_381_out,
       not_382_out, not_383_out, not_384_out, not_385_out, not_386_out, not_387_out, not_388_out,
       not_389_out, not_390_out, not_391_out, not_392_out, not_393_out, not_394_out, not_395_out,
       not_396_out, not_397_out, not_398_out, not_399_out, not_400_out, not_401_out, not_402_out,
       not_403_out, not_404_out, not_405_out, not_406_out, not_407_out, not_408_out, not_409_out,
       not_410_out, not_411_out, not_412_out, not_413_out, not_414_out;

  not not_1 (not_1_out, OP4);
  not not_2 (not_2_out, OP3);
  not not_3 (not_3_out, OP2);
  not not_4 (not_4_out, OP4);
  not not_5 (not_5_out, OP2);
  not not_6 (not_6_out, OP5);
  not not_7 (not_7_out, OP4);
  not not_8 (not_8_out, OP2);
  not not_9 (not_9_out, OP1);
  not not_10 (not_10_out, OP0);
  not not_11 (not_11_out, OP5);
  not not_12 (not_12_out, OP4);
  not not_13 (not_13_out, OP1);
  not not_14 (not_14_out, OP0);
  not not_15 (not_15_out, OP5);
  not not_16 (not_16_out, OP4);
  not not_17 (not_17_out, OP2);
  not not_18 (not_18_out, OP1);
  not not_19 (not_19_out, OP5);
  not not_20 (not_20_out, OP4);
  not not_21 (not_21_out, OP2);
  not not_22 (not_22_out, OP0);
  not not_23 (not_23_out, OP5);
  not not_24 (not_24_out, OP4);
  not not_25 (not_25_out, OP1);
  not not_26 (not_26_out, OP4);
  not not_27 (not_27_out, OP3);
  not not_28 (not_28_out, OP2);
  not not_29 (not_29_out, OP4);
  not not_30 (not_30_out, OP2);
  not not_31 (not_31_out, OP5);
  not not_32 (not_32_out, OP4);
  not not_33 (not_33_out, OP3);
  not not_34 (not_34_out, OP2);
  not not_35 (not_35_out, OP1);
  not not_36 (not_36_out, OP0);
  not not_37 (not_37_out, F5);
  not not_38 (not_38_out, F4);
  not not_39 (not_39_out, F3);
  not not_40 (not_40_out, F2);
  not not_41 (not_41_out, F1);
  not not_42 (not_42_out, F0);
  not not_43 (not_43_out, OP5);
  not not_44 (not_44_out, OP4);
  not not_45 (not_45_out, OP3);
  not not_46 (not_46_out, OP2);
  not not_47 (not_47_out, OP1);
  not not_48 (not_48_out, OP0);
  not not_49 (not_49_out, F5);
  not not_50 (not_50_out, F4);
  not not_51 (not_51_out, F3);
  not not_52 (not_52_out, F2);
  not not_53 (not_53_out, OP5);
  not not_54 (not_54_out, OP4);
  not not_55 (not_55_out, OP3);
  not not_56 (not_56_out, OP2);
  not not_57 (not_57_out, OP1);
  not not_58 (not_58_out, OP0);
  not not_59 (not_59_out, F5);
  not not_60 (not_60_out, F4);
  not not_61 (not_61_out, F3);
  not not_62 (not_62_out, F2);
  not not_63 (not_63_out, F0);
  not not_64 (not_64_out, OP5);
  not not_65 (not_65_out, OP4);
  not not_66 (not_66_out, OP3);
  not not_67 (not_67_out, OP2);
  not not_68 (not_68_out, OP1);
  not not_69 (not_69_out, OP0);
  not not_70 (not_70_out, F4);
  not not_71 (not_71_out, F3);
  not not_72 (not_72_out, F2);
  not not_73 (not_73_out, F1);
  not not_74 (not_74_out, F0);
  not not_75 (not_75_out, OP5);
  not not_76 (not_76_out, OP4);
  not not_77 (not_77_out, OP3);
  not not_78 (not_78_out, OP2);
  not not_79 (not_79_out, OP1);
  not not_80 (not_80_out, OP0);
  not not_81 (not_81_out, F4);
  not not_82 (not_82_out, F3);
  not not_83 (not_83_out, F2);
  not not_84 (not_84_out, F1);
  not not_85 (not_85_out, OP5);
  not not_86 (not_86_out, OP4);
  not not_87 (not_87_out, OP3);
  not not_88 (not_88_out, OP2);
  not not_89 (not_89_out, OP1);
  not not_90 (not_90_out, OP0);
  not not_91 (not_91_out, F4);
  not not_92 (not_92_out, F3);
  not not_93 (not_93_out, F2);
  not not_94 (not_94_out, F0);
  not not_95 (not_95_out, OP5);
  not not_96 (not_96_out, OP4);
  not not_97 (not_97_out, OP3);
  not not_98 (not_98_out, OP2);
  not not_99 (not_99_out, OP1);
  not not_100 (not_100_out, OP0);
  not not_101 (not_101_out, F4);
  not not_102 (not_102_out, F3);
  not not_103 (not_103_out, F1);
  not not_104 (not_104_out, F0);
  not not_105 (not_105_out, OP5);
  not not_106 (not_106_out, OP4);
  not not_107 (not_107_out, OP3);
  not not_108 (not_108_out, OP2);
  not not_109 (not_109_out, OP1);
  not not_110 (not_110_out, OP0);
  not not_111 (not_111_out, F4);
  not not_112 (not_112_out, F3);
  not not_113 (not_113_out, F1);
  not not_114 (not_114_out, OP5);
  not not_115 (not_115_out, OP4);
  not not_116 (not_116_out, OP3);
  not not_117 (not_117_out, OP2);
  not not_118 (not_118_out, OP1);
  not not_119 (not_119_out, OP0);
  not not_120 (not_120_out, F4);
  not not_121 (not_121_out, F3);
  not not_122 (not_122_out, OP5);
  not not_123 (not_123_out, OP4);
  not not_124 (not_124_out, OP3);
  not not_125 (not_125_out, OP2);
  not not_126 (not_126_out, OP1);
  not not_127 (not_127_out, OP0);
  not not_128 (not_128_out, F4);
  not not_129 (not_129_out, F2);
  not not_130 (not_130_out, F0);
  not not_131 (not_131_out, OP5);
  not not_132 (not_132_out, OP4);
  not not_133 (not_133_out, OP3);
  not not_134 (not_134_out, OP2);
  not not_135 (not_135_out, OP1);
  not not_136 (not_136_out, OP0);
  not not_137 (not_137_out, F4);
  not not_138 (not_138_out, F2);
  not not_139 (not_139_out, OP5);
  not not_140 (not_140_out, OP4);
  not not_141 (not_141_out, OP3);
  not not_142 (not_142_out, OP2);
  not not_143 (not_143_out, OP5);
  not not_144 (not_144_out, OP4);
  not not_145 (not_145_out, OP2);
  not not_146 (not_146_out, OP1);
  not not_147 (not_147_out, OP0);
  not not_148 (not_148_out, OP5);
  not not_149 (not_149_out, OP4);
  not not_150 (not_150_out, OP1);
  not not_151 (not_151_out, OP0);
  not not_152 (not_152_out, OP5);
  not not_153 (not_153_out, OP4);
  not not_154 (not_154_out, OP2);
  not not_155 (not_155_out, OP1);
  not not_156 (not_156_out, OP5);
  not not_157 (not_157_out, OP4);
  not not_158 (not_158_out, OP2);
  not not_159 (not_159_out, OP0);
  not not_160 (not_160_out, OP5);
  not not_161 (not_161_out, OP4);
  not not_162 (not_162_out, OP1);
  not not_163 (not_163_out, OP4);
  not not_164 (not_164_out, OP3);
  not not_165 (not_165_out, OP2);
  not not_166 (not_166_out, OP5);
  not not_167 (not_167_out, OP4);
  not not_168 (not_168_out, OP3);
  not not_169 (not_169_out, OP2);
  not not_170 (not_170_out, OP1);
  not not_171 (not_171_out, OP0);
  not not_172 (not_172_out, F5);
  not not_173 (not_173_out, F4);
  not not_174 (not_174_out, F3);
  not not_175 (not_175_out, F1);
  not not_176 (not_176_out, F0);
  not not_177 (not_177_out, OP5);
  not not_178 (not_178_out, OP4);
  not not_179 (not_179_out, OP3);
  not not_180 (not_180_out, OP2);
  not not_181 (not_181_out, OP1);
  not not_182 (not_182_out, OP0);
  not not_183 (not_183_out, F5);
  not not_184 (not_184_out, F4);
  not not_185 (not_185_out, F3);
  not not_186 (not_186_out, F0);
  not not_187 (not_187_out, OP4);
  not not_188 (not_188_out, OP2);
  not not_189 (not_189_out, OP1);
  not not_190 (not_190_out, OP0);
  not not_191 (not_191_out, OP5);
  not not_192 (not_192_out, OP4);
  not not_193 (not_193_out, OP3);
  not not_194 (not_194_out, OP2);
  not not_195 (not_195_out, OP1);
  not not_196 (not_196_out, OP0);
  not not_197 (not_197_out, F5);
  not not_198 (not_198_out, F4);
  not not_199 (not_199_out, F1);
  not not_200 (not_200_out, F0);
  not not_201 (not_201_out, OP5);
  not not_202 (not_202_out, OP4);
  not not_203 (not_203_out, OP3);
  not not_204 (not_204_out, OP1);
  not not_205 (not_205_out, OP0);
  not not_206 (not_206_out, OP5);
  not not_207 (not_207_out, OP4);
  not not_208 (not_208_out, OP3);
  not not_209 (not_209_out, OP1);
  not not_210 (not_210_out, OP5);
  not not_211 (not_211_out, OP4);
  not not_212 (not_212_out, OP2);
  not not_213 (not_213_out, OP1);
  not not_214 (not_214_out, OP0);
  not not_215 (not_215_out, OP5);
  not not_216 (not_216_out, OP4);
  not not_217 (not_217_out, OP2);
  not not_218 (not_218_out, OP1);
  not not_219 (not_219_out, OP5);
  not not_220 (not_220_out, OP4);
  not not_221 (not_221_out, OP2);
  not not_222 (not_222_out, OP0);
  not not_223 (not_223_out, OP4);
  not not_224 (not_224_out, OP3);
  not not_225 (not_225_out, OP2);
  not not_226 (not_226_out, OP4);
  not not_227 (not_227_out, OP2);
  not not_228 (not_228_out, OP5);
  not not_229 (not_229_out, OP4);
  not not_230 (not_230_out, OP3);
  not not_231 (not_231_out, OP5);
  not not_232 (not_232_out, OP4);
  not not_233 (not_233_out, OP3);
  not not_234 (not_234_out, OP2);
  not not_235 (not_235_out, OP1);
  not not_236 (not_236_out, OP0);
  not not_237 (not_237_out, F5);
  not not_238 (not_238_out, F4);
  not not_239 (not_239_out, F3);
  not not_240 (not_240_out, F2);
  not not_241 (not_241_out, F1);
  not not_242 (not_242_out, F0);
  not not_243 (not_243_out, OP5);
  not not_244 (not_244_out, OP4);
  not not_245 (not_245_out, OP3);
  not not_246 (not_246_out, OP2);
  not not_247 (not_247_out, OP1);
  not not_248 (not_248_out, OP0);
  not not_249 (not_249_out, F5);
  not not_250 (not_250_out, F4);
  not not_251 (not_251_out, F3);
  not not_252 (not_252_out, F2);
  not not_253 (not_253_out, OP5);
  not not_254 (not_254_out, OP4);
  not not_255 (not_255_out, OP3);
  not not_256 (not_256_out, OP2);
  not not_257 (not_257_out, OP1);
  not not_258 (not_258_out, OP0);
  not not_259 (not_259_out, F5);
  not not_260 (not_260_out, F4);
  not not_261 (not_261_out, F3);
  not not_262 (not_262_out, F2);
  not not_263 (not_263_out, F0);
  not not_264 (not_264_out, OP5);
  not not_265 (not_265_out, OP4);
  not not_266 (not_266_out, OP3);
  not not_267 (not_267_out, OP2);
  not not_268 (not_268_out, OP1);
  not not_269 (not_269_out, OP0);
  not not_270 (not_270_out, F4);
  not not_271 (not_271_out, F3);
  not not_272 (not_272_out, F2);
  not not_273 (not_273_out, F1);
  not not_274 (not_274_out, F0);
  not not_275 (not_275_out, OP5);
  not not_276 (not_276_out, OP4);
  not not_277 (not_277_out, OP3);
  not not_278 (not_278_out, OP2);
  not not_279 (not_279_out, OP1);
  not not_280 (not_280_out, OP0);
  not not_281 (not_281_out, F4);
  not not_282 (not_282_out, F3);
  not not_283 (not_283_out, F2);
  not not_284 (not_284_out, F1);
  not not_285 (not_285_out, OP5);
  not not_286 (not_286_out, OP4);
  not not_287 (not_287_out, OP3);
  not not_288 (not_288_out, OP2);
  not not_289 (not_289_out, OP1);
  not not_290 (not_290_out, OP0);
  not not_291 (not_291_out, F4);
  not not_292 (not_292_out, F3);
  not not_293 (not_293_out, F2);
  not not_294 (not_294_out, F0);
  not not_295 (not_295_out, OP5);
  not not_296 (not_296_out, OP4);
  not not_297 (not_297_out, OP3);
  not not_298 (not_298_out, OP2);
  not not_299 (not_299_out, OP1);
  not not_300 (not_300_out, OP0);
  not not_301 (not_301_out, F4);
  not not_302 (not_302_out, F3);
  not not_303 (not_303_out, F1);
  not not_304 (not_304_out, F0);
  not not_305 (not_305_out, OP5);
  not not_306 (not_306_out, OP4);
  not not_307 (not_307_out, OP3);
  not not_308 (not_308_out, OP2);
  not not_309 (not_309_out, OP1);
  not not_310 (not_310_out, OP0);
  not not_311 (not_311_out, F4);
  not not_312 (not_312_out, F3);
  not not_313 (not_313_out, F1);
  not not_314 (not_314_out, OP5);
  not not_315 (not_315_out, OP4);
  not not_316 (not_316_out, OP3);
  not not_317 (not_317_out, OP2);
  not not_318 (not_318_out, OP1);
  not not_319 (not_319_out, OP0);
  not not_320 (not_320_out, F4);
  not not_321 (not_321_out, F3);
  not not_322 (not_322_out, OP5);
  not not_323 (not_323_out, OP4);
  not not_324 (not_324_out, OP3);
  not not_325 (not_325_out, OP2);
  not not_326 (not_326_out, OP1);
  not not_327 (not_327_out, OP0);
  not not_328 (not_328_out, F4);
  not not_329 (not_329_out, F2);
  not not_330 (not_330_out, F0);
  not not_331 (not_331_out, OP5);
  not not_332 (not_332_out, OP4);
  not not_333 (not_333_out, OP3);
  not not_334 (not_334_out, OP2);
  not not_335 (not_335_out, OP1);
  not not_336 (not_336_out, OP0);
  not not_337 (not_337_out, F4);
  not not_338 (not_338_out, F2);
  not not_339 (not_339_out, OP5);
  not not_340 (not_340_out, OP4);
  not not_341 (not_341_out, OP3);
  not not_342 (not_342_out, OP2);
  not not_343 (not_343_out, OP1);
  not not_344 (not_344_out, OP0);
  not not_345 (not_345_out, F5);
  not not_346 (not_346_out, F4);
  not not_347 (not_347_out, F2);
  not not_348 (not_348_out, F1);
  not not_349 (not_349_out, F0);
  not not_350 (not_350_out, OP5);
  not not_351 (not_351_out, OP4);
  not not_352 (not_352_out, OP3);
  not not_353 (not_353_out, OP2);
  not not_354 (not_354_out, OP1);
  not not_355 (not_355_out, OP0);
  not not_356 (not_356_out, F5);
  not not_357 (not_357_out, F4);
  not not_358 (not_358_out, F3);
  not not_359 (not_359_out, F1);
  not not_360 (not_360_out, F0);
  not not_361 (not_361_out, OP5);
  not not_362 (not_362_out, OP4);
  not not_363 (not_363_out, OP3);
  not not_364 (not_364_out, OP2);
  not not_365 (not_365_out, OP1);
  not not_366 (not_366_out, OP0);
  not not_367 (not_367_out, F5);
  not not_368 (not_368_out, F4);
  not not_369 (not_369_out, F3);
  not not_370 (not_370_out, F0);
  not not_371 (not_371_out, OP5);
  not not_372 (not_372_out, OP4);
  not not_373 (not_373_out, OP3);
  not not_374 (not_374_out, OP1);
  not not_375 (not_375_out, OP0);
  not not_376 (not_376_out, OP5);
  not not_377 (not_377_out, OP4);
  not not_378 (not_378_out, OP3);
  not not_379 (not_379_out, OP1);
  not not_380 (not_380_out, OP5);
  not not_381 (not_381_out, OP4);
  not not_382 (not_382_out, OP3);
  not not_383 (not_383_out, OP2);
  not not_384 (not_384_out, OP1);
  not not_385 (not_385_out, OP0);
  not not_386 (not_386_out, F5);
  not not_387 (not_387_out, F4);
  not not_388 (not_388_out, F2);
  not not_389 (not_389_out, F1);
  not not_390 (not_390_out, F0);
  not not_391 (not_391_out, OP5);
  not not_392 (not_392_out, OP4);
  not not_393 (not_393_out, OP3);
  not not_394 (not_394_out, OP2);
  not not_395 (not_395_out, OP1);
  not not_396 (not_396_out, OP0);
  not not_397 (not_397_out, F5);
  not not_398 (not_398_out, F4);
  not not_399 (not_399_out, F2);
  not not_400 (not_400_out, F1);
  not not_401 (not_401_out, F0);
  not not_402 (not_402_out, OP5);
  not not_403 (not_403_out, OP4);
  not not_404 (not_404_out, OP3);
  not not_405 (not_405_out, OP2);
  not not_406 (not_406_out, OP0);
  not not_407 (not_407_out, OP5);
  not not_408 (not_408_out, OP4);
  not not_409 (not_409_out, OP3);
  not not_410 (not_410_out, OP2);
  not not_411 (not_411_out, OP5);
  not not_412 (not_412_out, OP4);
  not not_413 (not_413_out, OP3);
  not not_414 (not_414_out, OP2);
  and and_1 (MemToReg, OP5, not_1_out, not_2_out, not_3_out, OP1, OP0);
  and and_2 (MemWrite, OP5, not_4_out, OP3, not_5_out, OP1, OP0);
  and and_3 (and_3_out, not_6_out, not_7_out, OP3, not_8_out, not_9_out, not_10_out);
  and and_4 (and_4_out, not_11_out, not_12_out, OP3, OP2, not_13_out, not_14_out);
  and and_5 (and_5_out, not_15_out, not_16_out, OP3, not_17_out, not_18_out, OP0);
  and and_6 (and_6_out, not_19_out, not_20_out, OP3, not_21_out, OP1, not_22_out);
  and and_7 (and_7_out, not_23_out, not_24_out, OP3, OP2, not_25_out, OP0);
  and and_8 (and_8_out, OP5, not_26_out, not_27_out, not_28_out, OP1, OP0);
  and and_9 (and_9_out, OP5, not_29_out, OP3, not_30_out, OP1, OP0);
  and and_10 (and_10_out, not_31_out, not_32_out, not_33_out, not_34_out, not_35_out, not_36_out, not_37_out, not_38_out, not_39_out, not_40_out, not_41_out, not_42_out);
  and and_11 (and_11_out, not_43_out, not_44_out, not_45_out, not_46_out, not_47_out, not_48_out, not_49_out, not_50_out, not_51_out, not_52_out, F1, F0);
  and and_12 (and_12_out, not_53_out, not_54_out, not_55_out, not_56_out, not_57_out, not_58_out, not_59_out, not_60_out, not_61_out, not_62_out, F1, not_63_out);
  and and_13 (and_13_out, not_64_out, not_65_out, not_66_out, not_67_out, not_68_out, not_69_out, F5, not_70_out, not_71_out, not_72_out, not_73_out, not_74_out);
  and and_14 (and_14_out, not_75_out, not_76_out, not_77_out, not_78_out, not_79_out, not_80_out, F5, not_81_out, not_82_out, not_83_out, not_84_out, F0);
  and and_15 (and_15_out, not_85_out, not_86_out, not_87_out, not_88_out, not_89_out, not_90_out, F5, not_91_out, not_92_out, not_93_out, F1, not_94_out);
  and and_16 (and_16_out, not_95_out, not_96_out, not_97_out, not_98_out, not_99_out, not_100_out, F5, not_101_out, not_102_out, F2, not_103_out, not_104_out);
  and and_17 (and_17_out, not_105_out, not_106_out, not_107_out, not_108_out, not_109_out, not_110_out, F5, not_111_out, not_112_out, F2, not_113_out, F0);
  and and_18 (and_18_out, not_114_out, not_115_out, not_116_out, not_117_out, not_118_out, not_119_out, F5, not_120_out, not_121_out, F2, F1, F0);
  and and_19 (and_19_out, not_122_out, not_123_out, not_124_out, not_125_out, not_126_out, not_127_out, F5, not_128_out, F3, not_129_out, F1, not_130_out);
  and and_20 (and_20_out, not_131_out, not_132_out, not_133_out, not_134_out, not_135_out, not_136_out, F5, not_137_out, F3, not_138_out, F1, F0);
  and and_21 (and_21_out, not_139_out, not_140_out, not_141_out, not_142_out, OP1, OP0);
  and and_22 (and_22_out, not_143_out, not_144_out, OP3, not_145_out, not_146_out, not_147_out);
  and and_23 (and_23_out, not_148_out, not_149_out, OP3, OP2, not_150_out, not_151_out);
  and and_24 (and_24_out, not_152_out, not_153_out, OP3, not_154_out, not_155_out, OP0);
  and and_25 (and_25_out, not_156_out, not_157_out, OP3, not_158_out, OP1, not_159_out);
  and and_26 (and_26_out, not_160_out, not_161_out, OP3, OP2, not_162_out, OP0);
  and and_27 (and_27_out, OP5, not_163_out, not_164_out, not_165_out, OP1, OP0);
  and and_28 (and_28_out, not_166_out, not_167_out, not_168_out, not_169_out, not_170_out, not_171_out, not_172_out, not_173_out, not_174_out, F2, not_175_out, not_176_out);
  and and_29 (and_29_out, not_177_out, not_178_out, not_179_out, not_180_out, not_181_out, not_182_out, not_183_out, not_184_out, not_185_out, F2, F1, not_186_out);
  and and_30 (and_30_out, OP5, not_187_out, OP3, not_188_out, not_189_out, not_190_out);
  and and_31 (SysCALL, not_191_out, not_192_out, not_193_out, not_194_out, not_195_out, not_196_out, not_197_out, not_198_out, F3, F2, not_199_out, not_200_out);
  and and_32 (and_32_out, not_201_out, not_202_out, not_203_out, OP2, not_204_out, not_205_out);
  and and_33 (and_33_out, not_206_out, not_207_out, not_208_out, OP2, not_209_out, OP0);
  and and_34 (and_34_out, not_210_out, not_211_out, OP3, not_212_out, not_213_out, not_214_out);
  and and_35 (and_35_out, not_215_out, not_216_out, OP3, not_217_out, not_218_out, OP0);
  and and_36 (and_36_out, not_219_out, not_220_out, OP3, not_221_out, OP1, not_222_out);
  and and_37 (and_37_out, OP5, not_223_out, not_224_out, not_225_out, OP1, OP0);
  and and_38 (and_38_out, OP5, not_226_out, OP3, not_227_out, OP1, OP0);
  and and_39 (and_39_out, not_228_out, not_229_out, not_230_out, OP2, OP1, OP0);
  and and_40 (and_40_out, not_231_out, not_232_out, not_233_out, not_234_out, not_235_out, not_236_out, not_237_out, not_238_out, not_239_out, not_240_out, not_241_out, not_242_out);
  and and_41 (and_41_out, not_243_out, not_244_out, not_245_out, not_246_out, not_247_out, not_248_out, not_249_out, not_250_out, not_251_out, not_252_out, F1, F0);
  and and_42 (and_42_out, not_253_out, not_254_out, not_255_out, not_256_out, not_257_out, not_258_out, not_259_out, not_260_out, not_261_out, not_262_out, F1, not_263_out);
  and and_43 (and_43_out, not_264_out, not_265_out, not_266_out, not_267_out, not_268_out, not_269_out, F5, not_270_out, not_271_out, not_272_out, not_273_out, not_274_out);
  and and_44 (and_44_out, not_275_out, not_276_out, not_277_out, not_278_out, not_279_out, not_280_out, F5, not_281_out, not_282_out, not_283_out, not_284_out, F0);
  and and_45 (and_45_out, not_285_out, not_286_out, not_287_out, not_288_out, not_289_out, not_290_out, F5, not_291_out, not_292_out, not_293_out, F1, not_294_out);
  and and_46 (and_46_out, not_295_out, not_296_out, not_297_out, not_298_out, not_299_out, not_300_out, F5, not_301_out, not_302_out, F2, not_303_out, not_304_out);
  and and_47 (and_47_out, not_305_out, not_306_out, not_307_out, not_308_out, not_309_out, not_310_out, F5, not_311_out, not_312_out, F2, not_313_out, F0);
  and and_48 (and_48_out, not_314_out, not_315_out, not_316_out, not_317_out, not_318_out, not_319_out, F5, not_320_out, not_321_out, F2, F1, F0);
  and and_49 (and_49_out, not_322_out, not_323_out, not_324_out, not_325_out, not_326_out, not_327_out, F5, not_328_out, F3, not_329_out, F1, not_330_out);
  and and_50 (and_50_out, not_331_out, not_332_out, not_333_out, not_334_out, not_335_out, not_336_out, F5, not_337_out, F3, not_338_out, F1, F0);
  and and_51 (and_51_out, not_339_out, not_340_out, not_341_out, not_342_out, not_343_out, not_344_out, not_345_out, not_346_out, F3, not_347_out, not_348_out, not_349_out);
  and and_52 (and_52_out, not_350_out, not_351_out, not_352_out, not_353_out, not_354_out, not_355_out, not_356_out, not_357_out, not_358_out, F2, not_359_out, not_360_out);
  and and_53 (and_53_out, not_361_out, not_362_out, not_363_out, not_364_out, not_365_out, not_366_out, not_367_out, not_368_out, not_369_out, F2, F1, not_370_out);
  and and_54 (BEQ, not_371_out, not_372_out, not_373_out, OP2, not_374_out, not_375_out);
  and and_55 (BNE, not_376_out, not_377_out, not_378_out, OP2, not_379_out, OP0);
  and and_56 (JR, not_380_out, not_381_out, not_382_out, not_383_out, not_384_out, not_385_out, not_386_out, not_387_out, F3, not_388_out, not_389_out, not_390_out);
  and and_57 (and_57_out, not_391_out, not_392_out, not_393_out, not_394_out, not_395_out, not_396_out, not_397_out, not_398_out, F3, not_399_out, not_400_out, not_401_out);
  and and_58 (and_58_out, not_402_out, not_403_out, not_404_out, not_405_out, OP1, not_406_out);
  and and_59 (and_59_out, not_407_out, not_408_out, not_409_out, not_410_out, OP1, OP0);
  and and_60 (JAL, not_411_out, not_412_out, not_413_out, not_414_out, OP1, OP0);
  or or_1 (ALU_SRC, and_3_out, and_4_out, and_5_out, and_6_out, and_7_out, and_8_out, and_9_out);
  or or_2 (SignedExt, and_32_out, and_33_out, and_34_out, and_35_out, and_36_out, and_37_out, and_38_out, and_39_out);
  or or_3 (JUMP, and_57_out, and_58_out, and_59_out);
  or or_4 (RegWrite, and_10_out, and_11_out, and_12_out, and_13_out, and_14_out, and_15_out, and_16_out, and_17_out, and_18_out, and_19_out, and_20_out, and_21_out, and_22_out, and_23_out, and_24_out, and_25_out, and_26_out, and_27_out, and_28_out, and_29_out, and_30_out);
  or or_5 (RegDst, and_40_out, and_41_out, and_42_out, and_43_out, and_44_out, and_45_out, and_46_out, and_47_out, and_48_out, and_49_out, and_50_out, and_51_out, and_52_out, and_53_out);
endmodule

// 控制信号生成(扩展)
module \扩展_控制信号自动生成_4_三级中断  (
  input  OP0,
  input  OP1,
  input  OP2,
  input  OP3,
  input  OP4,
  input  OP5,
  input  F0,
  input  F1,
  input  F2,
  input  F3,
  input  F4,
  input  F5,
  output VarShift,
  output StoreByte,
  output BGTZ,
  output ERET,
  output MFC0
);

  wire and_1_out, and_2_out, and_6_out, and_7_out, not_1_out, not_2_out, not_3_out, not_4_out, not_5_out,
       not_6_out, not_7_out, not_8_out, not_9_out, not_10_out, not_11_out, not_12_out, not_13_out,
       not_14_out, not_15_out, not_16_out, not_17_out, not_18_out, not_19_out, not_20_out, not_21_out,
       not_22_out, not_23_out, not_24_out, not_25_out, not_26_out, not_27_out, not_28_out, not_29_out,
       not_30_out, not_31_out, not_32_out, not_33_out, not_34_out, not_35_out, not_36_out, not_37_out,
       not_38_out, not_39_out, not_40_out, not_41_out, not_42_out, not_43_out, not_44_out, not_45_out,
       not_46_out, not_47_out, not_48_out, not_49_out, not_50_out, not_51_out, not_52_out, not_53_out,
       not_54_out, not_55_out, not_56_out, not_57_out, not_58_out;

  not not_1 (not_1_out, OP5);
  not not_2 (not_2_out, OP4);
  not not_3 (not_3_out, OP3);
  not not_4 (not_4_out, OP2);
  not not_5 (not_5_out, OP1);
  not not_6 (not_6_out, OP0);
  not not_7 (not_7_out, F5);
  not not_8 (not_8_out, F4);
  not not_9 (not_9_out, F3);
  not not_10 (not_10_out, F1);
  not not_11 (not_11_out, F0);
  not not_12 (not_12_out, OP5);
  not not_13 (not_13_out, OP4);
  not not_14 (not_14_out, OP3);
  not not_15 (not_15_out, OP2);
  not not_16 (not_16_out, OP1);
  not not_17 (not_17_out, OP0);
  not not_18 (not_18_out, F5);
  not not_19 (not_19_out, F4);
  not not_20 (not_20_out, F3);
  not not_21 (not_21_out, F0);
  not not_22 (not_22_out, OP4);
  not not_23 (not_23_out, OP2);
  not not_24 (not_24_out, OP1);
  not not_25 (not_25_out, OP0);
  not not_26 (not_26_out, OP5);
  not not_27 (not_27_out, OP4);
  not not_28 (not_28_out, OP3);
  not not_29 (not_29_out, OP5);
  not not_30 (not_30_out, OP3);
  not not_31 (not_31_out, OP2);
  not not_32 (not_32_out, OP1);
  not not_33 (not_33_out, OP0);
  not not_34 (not_34_out, F5);
  not not_35 (not_35_out, F2);
  not not_36 (not_36_out, F1);
  not not_37 (not_37_out, F0);
  not not_38 (not_38_out, OP5);
  not not_39 (not_39_out, OP3);
  not not_40 (not_40_out, OP2);
  not not_41 (not_41_out, OP1);
  not not_42 (not_42_out, OP0);
  not not_43 (not_43_out, F5);
  not not_44 (not_44_out, F4);
  not not_45 (not_45_out, F3);
  not not_46 (not_46_out, F2);
  not not_47 (not_47_out, F1);
  not not_48 (not_48_out, F0);
  not not_49 (not_49_out, OP5);
  not not_50 (not_50_out, OP3);
  not not_51 (not_51_out, OP2);
  not not_52 (not_52_out, OP1);
  not not_53 (not_53_out, OP0);
  not not_54 (not_54_out, F5);
  not not_55 (not_55_out, F4);
  not not_56 (not_56_out, F3);
  not not_57 (not_57_out, F2);
  not not_58 (not_58_out, F1);
  and and_1 (and_1_out, not_1_out, not_2_out, not_3_out, not_4_out, not_5_out, not_6_out, not_7_out, not_8_out, not_9_out, F2, not_10_out, not_11_out);
  and and_2 (and_2_out, not_12_out, not_13_out, not_14_out, not_15_out, not_16_out, not_17_out, not_18_out, not_19_out, not_20_out, F2, F1, not_21_out);
  and and_3 (StoreByte, OP5, not_22_out, OP3, not_23_out, not_24_out, not_25_out);
  and and_4 (BGTZ, not_26_out, not_27_out, not_28_out, OP2, OP1, OP0);
  and and_5 (ERET, not_29_out, OP4, not_30_out, not_31_out, not_32_out, not_33_out, not_34_out, F4, F3, not_35_out, not_36_out, not_37_out);
  and and_6 (and_6_out, not_38_out, OP4, not_39_out, not_40_out, not_41_out, not_42_out, not_43_out, not_44_out, not_45_out, not_46_out, not_47_out, not_48_out);
  and and_7 (and_7_out, not_49_out, OP4, not_50_out, not_51_out, not_52_out, not_53_out, not_54_out, not_55_out, not_56_out, not_57_out, not_58_out, F0);
  or or_1 (VarShift, and_1_out, and_2_out);
  or or_2 (MFC0, and_6_out, and_7_out);
endmodule

module \MCOP辅助译码器  (
  input  MCOP,
  input  [4:0] RS,
  input  [4:0] RD,
  output MFEPC,
  output MTIE,
  output MTEPC
);

  wire comparator_1_eq, comparator_2_eq, comparator_3_eq, comparator_4_eq;

  Comparator #(.width(5), .mode("twosComplement")) comparator_1 (
    .a(RS), .b({5{1'b0}}), .eq(comparator_1_eq));  // open: gt, lt
  Comparator #(.width(5), .mode("twosComplement")) comparator_2 (
    .a(RS), .b(5'b00100), .eq(comparator_2_eq));  // open: gt, lt
  Comparator #(.width(5), .mode("twosComplement")) comparator_3 (
    .a(RD), .b(5'b01100), .eq(comparator_3_eq));  // open: gt, lt
  Comparator #(.width(5), .mode("twosComplement")) comparator_4 (
    .a(RD), .b(5'b01110), .eq(comparator_4_eq));  // open: gt, lt
  and and_1 (MFEPC, MCOP, comparator_1_eq, comparator_4_eq);
  and and_2 (MTIE, MCOP, comparator_2_eq, comparator_3_eq);
  and and_3 (MTEPC, MCOP, comparator_2_eq, comparator_4_eq);
endmodule

// ALU
module MIPS_ALU (
  input  [4:0] shamt,
  input  [31:0] X,
  input  [31:0] Y,
  input  [3:0] AluOP,
  output Equal,
  output [31:0] Result,
  output [31:0] Result_2
);

  wire [0:0] comparator_1_lt, comparator_2_lt;
  wire [31:0] adder_1_out, AND_out, divider_1_out, divider_1_rem, multiplier_1_cout, multiplier_1_out,
       NOR_out, OR_out, shifter_1_out, shifter_2_out, shifter_3_out, subtractor_1_out, XOR_out;

  assign AND_out = X & Y;  // AND_Gate AND, 32 bits wide
  assign OR_out = X | Y;  // OR_Gate OR, 32 bits wide
  Shifter #(.width(32), .shift("ll")) shifter_1 (.in(Y), .\dist (shamt), .out(shifter_1_out));
  Shifter #(.width(32), .shift("ar")) shifter_2 (.in(Y), .\dist (shamt), .out(shifter_2_out));
  Shifter #(.width(32), .shift("lr")) shifter_3 (.in(Y), .\dist (shamt), .out(shifter_3_out));
  Multiplier #(.width(32)) multiplier_1 (.a(X), .b(Y), .out(multiplier_1_out), .cout(multiplier_1_cout));  // open: cin
  Divider #(.width(32)) divider_1 (.a(X), .b(Y), .out(divider_1_out), .rem(divider_1_rem));  // open: upper
  Adder #(.width(32)) adder_1 (.a(X), .b(Y), .out(adder_1_out));  // open: cin, cout
  Subtractor #(.width(32)) subtractor_1 (.a(X), .b(Y), .out(subtractor_1_out));  // open: bin, bout
  assign XOR_out = X ^ Y;  // XOR_Gate XOR, 32 bits wide
  assign NOR_out = ~(X | Y);  // NOR_Gate NOR, 32 bits wide
  Comparator #(.width(32), .mode("twosComplement")) comparator_1 (
    .a(X), .b(Y), .eq(Equal), .lt(comparator_1_lt[0]));  // open: gt
  Comparator #(.width(32), .mode("unsigned")) comparator_2 (.a(X), .b(Y), .lt(comparator_2_lt[0]));  // open: gt, eq
  Multiplexer #(.select(4), .width(32), .disabled("Z"), .enable("false")) multiplexer_1 (
    .in0(shifter_1_out), .in1(shifter_2_out), .in2(shifter_3_out), .in3(multiplier_1_out),
    .in4(divider_1_out), .in5(adder_1_out), .in6(subtractor_1_out), .in7(AND_out), .in8(OR_out),
    .in9(XOR_out), .in10(NOR_out), .in11({{31{1'b0}}, comparator_1_lt[0]}),
    .in12({{31{1'b0}}, comparator_2_lt[0]}), .in13({32{1'b0}}), .in14({32{1'b0}}), .in15({32{1'b0}}),
    .out(Result), .sel(AluOP));
  Multiplexer #(.select(4), .width(32), .disabled("Z"), .enable("false")) multiplexer_2 (
    .in0({32{1'b0}}), .in1({32{1'b0}}), .in2({32{1'b0}}), .in3(multiplier_1_cout), .in4(divider_1_rem),
    .in5({32{1'b0}}), .in6({32{1'b0}}), .in7({32{1'b0}}), .in8({32{1'b0}}), .in9({32{1'b0}}),
    .in10({32{1'b0}}), .in11({32{1'b0}}), .in12({32{1'b0}}), .in13({32{1'b0}}), .in14({32{1'b0}}),
    .in15({32{1'b0}}), .out(Result_2), .sel(AluOP));

  // Other names for the same wires on the sheet: Result2[31:0] = Result_2; S[3:0] = AluOP

  // Notes on the sheet:
  //   不要改变此引脚区域内容，也不要改变ALU封装形式
  //   输入引脚
  //   输出引脚
endmodule

module MIPS_Regifile (
  input  [31:0] Din,
  input  Clk,
  input  WE,
  input  [4:0] R1_num,
  input  [4:0] W_num,
  input  [4:0] R2_num,
  output [31:0] R1,
  output [31:0] R2
);

  // RegisterFile registerfile_1: pin names not known; wires that end beside it: Din, Clk, WE, W_num, R1_num, R2_num, R1, R2
endmodule

module \中断按键参考电路  (
  input  \同步清零信号 ,
  output \与中断屏蔽位与 
);

  wire \_1号中断_out , and_1_out, clock_1_out, d_ff_1_q, or_1_out, or_2_out;

  Clock #(.highDuration(1), .lowDuration(1)) clock_1 (.out(clock_1_out));
  Button \_1号中断  (.out(\_1号中断_out ));
  LED #(.active("true")) \_1号中断等待指示灯  (.in(or_1_out));
  or or_1 (or_1_out, \与中断屏蔽位与 , d_ff_1_q);
  D_Flip_Flop #(.trigger("rising"), .Pre_Clr_Positions("LEGACY"), .NegatePresetClear("false"), .enable("true"), .NewFFLayout("false")) d_ff_1 (
    .clk(\_1号中断_out ), .D(1'b1), .Q(d_ff_1_q), .reset(\与中断屏蔽位与 ));  // open: Qn, preset, en
  or or_2 (or_2_out, d_ff_1_q, \与中断屏蔽位与 );
  and and_1 (and_1_out, or_2_out, ~\同步清零信号 );  // AND_Gate
  D_Flip_Flop #(.trigger("rising"), .Pre_Clr_Positions("LEGACY"), .NegatePresetClear("false"), .enable("true"), .NewFFLayout("false")) IR1 (
    .clk(clock_1_out), .D(and_1_out), .Q(\与中断屏蔽位与 ));  // open: Qn, preset, en, reset

  // Notes on the sheet:
  //   中断信号采样参考电路
  //   Reset 
endmodule
